// Logisim project 8bitcomputer.circ as structural Verilog: 50 circuits, main circuit main
module main (
  input  CLOCK,
  input  CONTINUE,
  input  RESET,
  output [15:0] out_4,
  output [3:0] out_5,
  output [3:0] out_6,
  output [7:0] out_7,
  output [15:0] out_8
);

  wire and_1_out, and_2_out, call_stack_16x16_1_write_enable, control_logic_unit_1_call,
       control_logic_unit_1_halt, control_logic_unit_1_jump, control_logic_unit_1_pop,
       control_logic_unit_1_push, control_logic_unit_1_rtrn, control_logic_unit_1_save_register,
       control_logic_unit_1_save_to_ram, control_logic_unit_1_save_video, not_1_out, not_2_out, or_1_out,
       push_pop_stack_256x8_1_write_enable, xnor_1_out;
  wire [3:0] call_stack_16x16_1_address, control_logic_unit_1_register_2_out;
  wire [7:0] INSTRUCTION_REGISTER_16X8_bit_data, push_pop_stack_256x8_1_address,
       push_pop_stack_256x8_1_out_8, ram_1_dout, RAM_8x8_bit_RAM_dout, sixteen_eight_register_1_output_a,
       sixteen_eight_register_1_output_b, sixteen_eight_register_1_r13, sixteen_eight_register_1_r14,
       sixteen_eight_register_1_r15;
  wire [15:0] call_stack_16x16_1_out_16, ram_2_dout;

  or or_1 (or_1_out, CONTINUE, xnor_1_out);
  xnor xnor_1 (xnor_1_out, CONTINUE, control_logic_unit_1_halt);
  and and_1 (and_1_out, CLOCK, or_1_out);
  and and_2 (and_2_out, RESET, ~and_1_out);  // AND_Gate
  SIXTEEN_BIT_PROGRAM_COUNTER sixteen_bit_program_counter_1 (
    .CLOCK(and_1_out), .RESET(and_2_out), .INP(out_8), .WRITE(control_logic_unit_1_jump), .COUNT(out_4));
  ROM #(.addrWidth(16)) INSTRUCTION_REGISTER_16X8_bit (.addr(out_4), .data(INSTRUCTION_REGISTER_16X8_bit_data));
  not not_1 (not_1_out, and_1_out);
  RAM RAM_8x8_bit_RAM (
    .addr(out_7), .we(control_logic_unit_1_save_to_ram), .oe(1'b1), .clk(and_1_out),
    .dout(RAM_8x8_bit_RAM_dout));  // open: din
  PUSH_POP_STACK_256x8 push_pop_stack_256x8_1 (
    .CLOCK(not_1_out), .INPUT_8(out_7), .PUSH(control_logic_unit_1_push), .POP(control_logic_unit_1_pop),
    .ADDRESS(push_pop_stack_256x8_1_address), .OUT_8(push_pop_stack_256x8_1_out_8),
    .WRITE_ENABLE(push_pop_stack_256x8_1_write_enable));
  RAM ram_1 (
    .addr(push_pop_stack_256x8_1_address), .we(push_pop_stack_256x8_1_write_enable), .oe(1'b1),
    .clk(not_1_out), .din(push_pop_stack_256x8_1_out_8), .dout(ram_1_dout));
  not not_2 (not_2_out, and_1_out);
  SIXTEEN_EIGHT_REGISTER sixteen_eight_register_1 (
    .RESET(RESET), .WRITE_Address(out_5), .INPUT_Data(out_7), .ENABLE(control_logic_unit_1_save_register),
    .CLOCK(not_2_out), .INPUT_ADDRESS_A(out_6), .INPUT_ADDRESS_B(control_logic_unit_1_register_2_out),
    .R13(sixteen_eight_register_1_r13), .R14(sixteen_eight_register_1_r14),
    .R15(sixteen_eight_register_1_r15), .OUTPUT_B(sixteen_eight_register_1_output_b),
    .OUTPUT_A(sixteen_eight_register_1_output_a));  // open: R2, R0, R1, R3, F4, F5, F6, R7, R8, R9, R10, R11, R12
  CONTROL_LOGIC_UNIT control_logic_unit_1 (
    .Clock(and_1_out), .RESET(RESET), .INSTRUCTION_BUS(INSTRUCTION_REGISTER_16X8_bit_data),
    .R1_IN(sixteen_eight_register_1_output_a), .R2_IN(sixteen_eight_register_1_output_b),
    .RAM_IN(RAM_8x8_bit_RAM_dout), .STACK_IN(ram_1_dout), .CALL_ADDRESS_IN(ram_2_dout),
    .HALT(control_logic_unit_1_halt), .SAVE_TO_RAM(control_logic_unit_1_save_to_ram),
    .SAVE_VIDEO(control_logic_unit_1_save_video), .SAVE_REGISTER(control_logic_unit_1_save_register),
    .RTRN(control_logic_unit_1_rtrn), .PUSH(control_logic_unit_1_push), .POP(control_logic_unit_1_pop),
    .REGISTER_DESTINATION(out_5), .REGISTER_1_OUT(out_6),
    .REGISTER_2_OUT(control_logic_unit_1_register_2_out), .RESULT(out_7), .CALL(control_logic_unit_1_call),
    .JUMP_ADDRESS(out_8), .JUMP(control_logic_unit_1_jump));  // open: out_17
  CALL_STACK_16x16 call_stack_16x16_1 (
    .CLOCK(not_1_out), .CALL(control_logic_unit_1_call), .RTRN(control_logic_unit_1_rtrn), .INPUT_16(out_8),
    .ADDRESS(call_stack_16x16_1_address), .OUT_16(call_stack_16x16_1_out_16),
    .WRITE_ENABLE(call_stack_16x16_1_write_enable));
  RAM #(.addrWidth(4), .dataWidth(16)) ram_2 (
    .addr(call_stack_16x16_1_address), .we(call_stack_16x16_1_write_enable), .oe(1'b1), .clk(not_1_out),
    .din(call_stack_16x16_1_out_16), .dout(ram_2_dout));
  // RGB_Video #(.cursor("No Cursor"), .height(64), .scale(4), .width(64)) rgb_video_1: pin names not known; wires that end beside it: RESET, not_1_out, control_logic_unit_1_save_video, sixteen_eight_register_1_r15[5:0], sixteen_eight_register_1_r14[5:0], sixteen_eight_register_1_r13

  // Notes on the sheet:
  //   contents of INSTRUCTION_REGISTER_16X8_bit (hex, n*v repeats v):
  //   5 d0 0 5 e0 0 5 f0 0 6 23 dd 23 ff 35 f0 40 2b 0 8 23 ee 35 e0 40 2b 0 5 1
  //   STACK OUT
  //   CALL ADDRESS
endmodule

module TWO_MUX (
  input  S0,
  input  F1,
  input  F0,
  output Y
);

  wire and_1_out, and_2_out, not_1_out;

  not not_1 (not_1_out, S0);
  and and_1 (and_1_out, S0, F1);
  and and_2 (and_2_out, not_1_out, F0);
  or or_1 (Y, and_1_out, and_2_out);
endmodule

module SIXTEEN_MUX (
  input  S0,
  input  S1,
  input  S2,
  input  S3,
  input  F15,
  input  F14,
  input  F13,
  input  F12,
  input  F11,
  input  F10,
  input  F9,
  input  F8,
  input  F7,
  input  F6,
  input  F5,
  input  F4,
  input  F3,
  input  F2,
  input  F1,
  input  F0,
  output Y
);

  wire four_mux_1_y, four_mux_2_y, four_mux_3_y, four_mux_4_y;

  FOUR_MUX four_mux_1 (.S0(S1), .S1(S0), .F3(F15), .F2(F14), .F1(F13), .F0(F12), .Y(four_mux_1_y));
  FOUR_MUX four_mux_2 (.S0(S1), .S1(S0), .F3(F11), .F2(F10), .F1(F9), .F0(F8), .Y(four_mux_2_y));
  FOUR_MUX four_mux_3 (.S0(S1), .S1(S0), .F3(F7), .F2(F6), .F1(F5), .F0(F4), .Y(four_mux_3_y));
  FOUR_MUX four_mux_4 (.S0(S1), .S1(S0), .F3(F3), .F2(F2), .F1(F1), .F0(F0), .Y(four_mux_4_y));
  FOUR_MUX four_mux_5 (
    .S0(S2), .S1(S3), .F3(four_mux_1_y), .F2(four_mux_2_y), .F1(four_mux_3_y), .F0(four_mux_4_y), .Y(Y));
endmodule

module TWO_DEMUX (
  input  G,
  input  S0,
  output F1,
  output F0
);

  wire not_1_out;

  not not_1 (not_1_out, S0);
  and and_1 (F1, G, not_1_out);
  and and_2 (F0, G, S0);
endmodule

module FOUR_MUX (
  input  S0,
  input  S1,
  input  F3,
  input  F2,
  input  F1,
  input  F0,
  output Y
);

  wire and_1_out, and_2_out, and_3_out, and_4_out, not_1_out, not_2_out;

  not not_1 (not_1_out, S0);
  not not_2 (not_2_out, S1);
  and and_1 (and_1_out, S0, S1, F3);
  and and_2 (and_2_out, S0, not_2_out, F2);
  and and_3 (and_3_out, S1, not_1_out, F1);
  and and_4 (and_4_out, not_2_out, not_1_out, F0);
  or or_1 (Y, and_1_out, and_2_out, and_3_out, and_4_out);
endmodule

module FOUR_DEMUX (
  input  G,
  input  S1,
  input  S0,
  output F3,
  output F2,
  output F1,
  output F0
);

  wire not_1_out, not_2_out;

  not not_1 (not_1_out, S1);
  not not_2 (not_2_out, S0);
  and and_1 (F3, G, S1, S0);
  and and_2 (F2, G, S1, not_2_out);
  and and_3 (F1, G, not_1_out, S0);
  and and_4 (F0, G, not_1_out, not_2_out);
endmodule

module SIXTEEN_DEMUX (
  input  G,
  input  S3,
  input  S2,
  input  S1,
  input  S0,
  output F15,
  output F14,
  output F13,
  output F12,
  output F11,
  output F10,
  output F9,
  output F8,
  output F7,
  output F6,
  output F5,
  output F4,
  output F3,
  output F2,
  output F1,
  output F0
);

  wire not_1_out, not_2_out, not_3_out, not_4_out;

  not not_1 (not_1_out, S3);
  not not_2 (not_2_out, S2);
  not not_3 (not_3_out, S1);
  not not_4 (not_4_out, S0);
  and and_1 (F15, G, S3, S2, S1, S0);
  and and_2 (F14, G, S3, S2, S1, not_4_out);
  and and_3 (F13, G, S3, S2, not_2_out, S0);
  and and_4 (F12, G, S3, S2, not_3_out, not_4_out);
  and and_5 (F11, G, S3, not_2_out, S1, S0);
  and and_6 (F10, G, S3, not_2_out, S1, not_4_out);
  and and_7 (F9, G, S3, not_2_out, not_3_out, S0);
  and and_8 (F8, G, S3, not_2_out, not_3_out, not_4_out);
  and and_9 (F7, G, not_1_out, S2, S1, S0);
  and and_10 (F6, G, not_1_out, S2, S1, not_4_out);
  and and_11 (F5, G, not_1_out, S2, not_3_out, S0);
  and and_12 (F4, G, not_1_out, S2, not_3_out, not_4_out);
  and and_13 (F3, G, not_1_out, not_2_out, S1, S0);
  and and_14 (F2, G, not_1_out, not_2_out, S1, not_4_out);
  and and_15 (F1, G, not_1_out, not_2_out, not_3_out, S0);
  and and_16 (F0, G, not_1_out, not_2_out, not_3_out, not_4_out);
endmodule

module FOUR_DECODER (
  input  S1,
  input  S0,
  output Y3,
  output Y2,
  output Y1,
  output Y0
);

  wire not_1_out, not_2_out;

  not not_1 (not_1_out, S1);
  not not_2 (not_2_out, S0);
  and and_1 (Y3, S1, S0);
  and and_2 (Y2, S1, not_2_out);
  and and_3 (Y1, not_1_out, S0);
  and and_4 (Y0, not_1_out, not_2_out);
endmodule

module EIGHT_DECODER (
  input  F2,
  input  F1,
  input  F0,
  output Y7,
  output Y6,
  output Y5,
  output Y4,
  output Y3,
  output Y2,
  output Y1,
  output Y0
);

  wire not_1_out, not_2_out, not_3_out;

  not not_1 (not_1_out, F2);
  not not_2 (not_2_out, F1);
  not not_3 (not_3_out, F0);
  and and_1 (Y7, F2, F1, F0);
  and and_2 (Y6, F2, F1, not_3_out);
  and and_3 (Y5, F2, not_2_out, F0);
  and and_4 (Y4, F2, not_2_out, not_3_out);
  and and_5 (Y3, not_1_out, F1, F0);
  and and_6 (Y2, not_1_out, F1, not_3_out);
  and and_7 (Y1, not_1_out, not_2_out, F0);
  and and_8 (Y0, not_3_out, not_2_out, not_1_out);
endmodule

module SIXTEEN_DECODER (
  input  F3,
  input  F2,
  input  F1,
  input  F0,
  output Y15,
  output Y14,
  output Y13,
  output Y12,
  output Y11,
  output Y10,
  output Y9,
  output Y8,
  output Y7,
  output Y6,
  output Y5,
  output Y4,
  output Y3,
  output Y2,
  output Y1,
  output Y0
);

  wire not_1_out, not_2_out, not_3_out, not_4_out;

  not not_1 (not_1_out, F3);
  not not_2 (not_2_out, F2);
  not not_3 (not_3_out, F1);
  not not_4 (not_4_out, F0);
  and and_1 (Y15, F3, F2, F1, F0);
  and and_2 (Y14, F3, F2, F1, not_4_out);
  and and_3 (Y13, F3, F2, not_3_out, F0);
  and and_4 (Y12, F3, F2, not_3_out, not_4_out);
  and and_5 (Y11, F3, not_2_out, F1, F0);
  and and_6 (Y10, F3, not_2_out, F1, not_4_out);
  and and_7 (Y9, F3, not_2_out, not_3_out, F0);
  and and_8 (Y8, F3, not_2_out, not_3_out, not_4_out);
  and and_9 (Y7, not_1_out, F2, F1, F0);
  and and_10 (Y6, not_1_out, F2, F1, not_4_out);
  and and_11 (Y5, not_1_out, F2, not_3_out, F0);
  and and_12 (Y4, not_1_out, F2, not_3_out, not_4_out);
  and and_13 (Y3, not_1_out, not_2_out, F1, F0);
  and and_14 (Y2, not_1_out, not_2_out, F1, not_4_out);
  and and_15 (Y1, not_1_out, not_2_out, not_3_out, F0);
  and and_16 (Y0, not_1_out, not_2_out, not_3_out, not_4_out);
endmodule

module D_LATCH (
  input  D,
  input  CLK,
  output Q,
  output NQ
);

  wire nand_1_out, nand_2_out, not_1_out;

  not not_1 (not_1_out, D);
  nand nand_1 (nand_1_out, D, CLK);
  nand nand_2 (nand_2_out, not_1_out, CLK);
  nand nand_3 (Q, nand_1_out, NQ);
  nand nand_4 (NQ, Q, nand_2_out);
endmodule

module T_LATCH (
  input  T,
  input  CLK,
  output Q,
  output NQ
);

  wire nand_1_out, nand_2_out;

  nand nand_1 (nand_1_out, NQ, T, CLK);
  nand nand_2 (nand_2_out, T, Q);
  nand nand_3 (Q, nand_1_out, NQ);
  nand nand_4 (NQ, Q, nand_2_out);
endmodule

module JK_LATCH (
  input  J,
  input  CLK,
  input  K,
  output Q,
  output NQ
);

  wire nand_1_out, nand_2_out;

  nand nand_1 (nand_1_out, NQ, J, CLK);
  nand nand_2 (nand_2_out, CLK, K, Q);
  nand nand_3 (Q, NQ, nand_1_out);
  nand nand_4 (NQ, nand_2_out, Q);
endmodule

module SR_LATCH (
  input  S,
  input  CLK,
  input  R,
  output Q,
  output NQ
);

  wire and_1_out, and_2_out;

  and and_1 (and_1_out, S, CLK);
  and and_2 (and_2_out, CLK, R);
  nor nor_1 (Q, NQ, and_1_out);
  nor nor_2 (NQ, and_2_out, Q);
endmodule

module EIGHT_BIT_REGISTER_RISING_EDGE (
  input  [7:0] DATA,
  input  WRITE,
  input  CLK,
  input  RESET,
  output [7:0] out_5
);

  wire and_1_out, and_2_out, and_3_out, and_4_out, and_5_out, and_6_out, and_7_out, and_8_out;

  D_Flip_Flop d_ff_1 (.D(and_1_out), .clk(CLK), .Q(out_5[0]), .reset(RESET));  // open: Qn, preset
  and and_1 (and_1_out, DATA[0], WRITE);
  D_Flip_Flop d_ff_2 (.D(and_2_out), .clk(CLK), .Q(out_5[1]), .reset(RESET));  // open: Qn, preset
  and and_2 (and_2_out, DATA[1], WRITE);
  D_Flip_Flop d_ff_3 (.D(and_3_out), .clk(CLK), .Q(out_5[2]), .reset(RESET));  // open: Qn, preset
  and and_3 (and_3_out, DATA[2], WRITE);
  D_Flip_Flop d_ff_4 (.D(and_4_out), .clk(CLK), .Q(out_5[3]), .reset(RESET));  // open: Qn, preset
  and and_4 (and_4_out, DATA[3], WRITE);
  D_Flip_Flop d_ff_5 (.D(and_5_out), .clk(CLK), .Q(out_5[4]), .reset(RESET));  // open: Qn, preset
  and and_5 (and_5_out, DATA[4], WRITE);
  D_Flip_Flop d_ff_6 (.D(and_6_out), .clk(CLK), .Q(out_5[5]), .reset(RESET));  // open: Qn, preset
  and and_6 (and_6_out, DATA[5], WRITE);
  D_Flip_Flop d_ff_7 (.D(and_7_out), .clk(CLK), .Q(out_5[6]), .reset(RESET));  // open: Qn, preset
  and and_7 (and_7_out, DATA[6], WRITE);
  D_Flip_Flop d_ff_8 (.D(and_8_out), .clk(CLK), .Q(out_5[7]), .reset(RESET));  // open: Qn, preset
  and and_8 (and_8_out, DATA[7], WRITE);
endmodule

module D_FLIP_FLOP_RISING_EDGE (
  input  PRESET,
  input  D,
  input  CLK,
  input  RESET,
  output Q,
  output NQ
);

  wire nand_1_out, nand_2_out, nand_3_out, nand_4_out, nand_5_out, nand_6_out, not_1_out, not_2_out;

  not not_1 (not_1_out, D);
  nand nand_1 (nand_1_out, D, CLK);
  nand nand_2 (nand_2_out, not_1_out, CLK);
  nand nand_3 (nand_3_out, PRESET, nand_1_out, nand_4_out);
  nand nand_4 (nand_4_out, nand_3_out, nand_2_out, RESET);
  not not_2 (not_2_out, CLK);
  nand nand_5 (nand_5_out, nand_3_out, not_2_out);
  nand nand_6 (nand_6_out, nand_4_out, not_2_out);
  nand nand_7 (Q, PRESET, nand_5_out, NQ);
  nand nand_8 (NQ, Q, nand_6_out, RESET);
endmodule

module FULL_ADDER (
  input  A,
  input  B,
  input  CIN,
  output SUM,
  output COUT
);

  wire and_1_out, and_2_out, xor_1_out;

  xor xor_1 (xor_1_out, A, B);
  xor xor_2 (SUM, xor_1_out, CIN);
  and and_1 (and_1_out, CIN, xor_1_out);
  and and_2 (and_2_out, B, A);
  or or_1 (COUT, and_1_out, and_2_out);
endmodule

module HALF_ADDER (
  input  A,
  input  SUM,
  input  B,
  input  COUT
);

  xor xor_1 (SUM, A, B);
  and and_1 (COUT, A, B);
endmodule

module HALF_SUBTRACTOR (
  input  A,
  input  DIFF,
  input  B,
  input  COUT
);

  wire not_1_out;

  not not_1 (not_1_out, A);
  and and_1 (COUT, not_1_out, B);
  xor xor_1 (DIFF, A, B);
endmodule

module FULL_SUBTRACTOR (
  input  A,
  input  B,
  input  CIN,
  output DIFF,
  output COUT
);

  wire and_1_out, and_2_out, and_3_out, not_1_out;

  not not_1 (not_1_out, A);
  and and_1 (and_1_out, B, CIN);
  and and_2 (and_2_out, not_1_out, B);
  and and_3 (and_3_out, not_1_out, CIN);
  ExactlyOne xor_1 (.out(DIFF), .in0(A), .in1(B), .in2(CIN));
  or or_1 (COUT, and_1_out, and_2_out, and_3_out);
endmodule

module EIGHT_BIT_ADD_SUB (
  input  [7:0] A,
  input  [7:0] B,
  input  K,
  input  CIN,
  output COUT,
  output [7:0] SUM
);

  wire full_adder_1_p2, full_adder_2_p2, full_adder_3_p2, full_adder_4_p2, full_adder_5_p2, full_adder_6_p2,
       full_adder_7_p2, xor_1_out, xor_2_out, xor_3_out, xor_4_out, xor_5_out, xor_6_out, xor_7_out,
       xor_8_out;

  xor xor_1 (xor_1_out, K, B[0]);
  // FULL_ADDER full_adder_1: pin names not known; wires that end beside it: SUM[7], full_adder_1_p2
  xor xor_2 (xor_2_out, K, B[1]);
  // FULL_ADDER full_adder_2: pin names not known; wires that end beside it: SUM[6], full_adder_2_p2
  xor xor_3 (xor_3_out, K, B[2]);
  // FULL_ADDER full_adder_3: pin names not known; wires that end beside it: SUM[5], full_adder_3_p2
  xor xor_4 (xor_4_out, K, B[3]);
  // FULL_ADDER full_adder_4: pin names not known; wires that end beside it: SUM[4], full_adder_4_p2
  xor xor_5 (xor_5_out, K, B[4]);
  // FULL_ADDER full_adder_5: pin names not known; wires that end beside it: SUM[3], full_adder_5_p2
  xor xor_6 (xor_6_out, K, B[5]);
  // FULL_ADDER full_adder_6: pin names not known; wires that end beside it: SUM[2], full_adder_6_p2
  xor xor_7 (xor_7_out, K, B[6]);
  // FULL_ADDER full_adder_7: pin names not known; wires that end beside it: SUM[1], full_adder_7_p2
  xor xor_8 (xor_8_out, K, B[7]);
  // FULL_ADDER full_adder_8: pin names not known; wires that end beside it: SUM[0], COUT
endmodule

module MULT_HELPER (
  input  [15:0] A,
  input  B,
  output [15:0] F1,
  output [15:0] F2
);

  Multiplexer #(.width(16)) multiplexer_1 (.in0({16{1'b0}}), .in1({A[14:0], 1'b0}), .out(F1), .sel(B));

  assign F2 = {A[14:0], 1'b0};
endmodule

module EIGHT_BIT_MULT (
  input  [7:0] A,
  input  [7:0] B,
  output [15:0] out_3
);

  wire adder_1_cout, adder_2_cout, adder_3_cout, adder_4_cout, adder_5_cout, adder_6_cout, adder_7_cout;
  wire [15:0] adder_1_out, adder_2_out, adder_3_out, adder_4_out, adder_5_out, adder_6_out, adder_7_out,
       mult_helper_1_f1, mult_helper_1_f2, mult_helper_2_f1, mult_helper_2_f2, mult_helper_3_f1,
       mult_helper_3_f2, mult_helper_4_f1, mult_helper_4_f2, mult_helper_5_f1, mult_helper_5_f2,
       mult_helper_6_f1, mult_helper_6_f2, mult_helper_7_f1, multiplexer_1_out;

  Multiplexer #(.width(16)) multiplexer_1 (.in0({16{1'b0}}), .in1({{8{1'b0}}, A}), .out(multiplexer_1_out), .sel(B[0]));
  MULT_HELPER mult_helper_1 (.A({{8{1'b0}}, A}), .B(B[1]), .F1(mult_helper_1_f1), .F2(mult_helper_1_f2));
  MULT_HELPER mult_helper_2 (.A(mult_helper_1_f2), .B(B[2]), .F1(mult_helper_2_f1), .F2(mult_helper_2_f2));
  MULT_HELPER mult_helper_3 (.A(mult_helper_2_f2), .B(B[3]), .F1(mult_helper_3_f1), .F2(mult_helper_3_f2));
  MULT_HELPER mult_helper_4 (.A(mult_helper_3_f2), .B(B[4]), .F1(mult_helper_4_f1), .F2(mult_helper_4_f2));
  MULT_HELPER mult_helper_5 (.A(mult_helper_4_f2), .B(B[5]), .F1(mult_helper_5_f1), .F2(mult_helper_5_f2));
  MULT_HELPER mult_helper_6 (.A(mult_helper_5_f2), .B(B[6]), .F1(mult_helper_6_f1), .F2(mult_helper_6_f2));
  MULT_HELPER mult_helper_7 (.A(mult_helper_6_f2), .B(B[7]), .F1(mult_helper_7_f1));  // open: F2
  Adder #(.width(16)) adder_1 (
    .a(multiplexer_1_out), .b({16{1'b0}}), .out(adder_1_out), .cout(adder_1_cout));  // open: cin
  Adder #(.width(16)) adder_2 (
    .a(mult_helper_1_f1), .b(adder_1_out), .out(adder_2_out), .cin(adder_1_cout), .cout(adder_2_cout));
  Adder #(.width(16)) adder_3 (
    .a(adder_2_out), .b(mult_helper_2_f1), .out(adder_3_out), .cin(adder_2_cout), .cout(adder_3_cout));
  Adder #(.width(16)) adder_4 (
    .a(adder_3_out), .b(mult_helper_3_f1), .out(adder_4_out), .cin(adder_3_cout), .cout(adder_4_cout));
  Adder #(.width(16)) adder_5 (
    .a(adder_4_out), .b(mult_helper_4_f1), .out(adder_5_out), .cin(adder_4_cout), .cout(adder_5_cout));
  Adder #(.width(16)) adder_6 (
    .a(adder_5_out), .b(mult_helper_5_f1), .out(adder_6_out), .cin(adder_5_cout), .cout(adder_6_cout));
  Adder #(.width(16)) adder_7 (
    .a(adder_6_out), .b(mult_helper_6_f1), .out(adder_7_out), .cin(adder_6_cout), .cout(adder_7_cout));
  Adder #(.width(16)) adder_8 (.a(adder_7_out), .b(mult_helper_7_f1), .out(out_3), .cin(adder_7_cout));  // open: cout
endmodule

module EIGHT_SHIFT_LEFT (
  input  [7:0] in_1,
  output [7:0] out_2
);


  assign out_2 = {in_1[6:0], 1'b0};
endmodule

module LOGICAL_RIGHT_SHIFT (
  input  [3:0] A,
  input  [1:0] SHIFT,
  output [3:0] O
);

  Multiplexer #(.select(2), .width(4)) multiplexer_1 (
    .in0(A), .in1({1'b0, A[3:1]}), .in2({2'b00, A[3:2]}), .in3({3'b000, A[3]}), .out(O), .sel(SHIFT));
endmodule

module LOGICAL_LEFT_SHIFT (
  input  [3:0] A,
  input  [1:0] SHIFT,
  output [3:0] O
);

  Multiplexer #(.select(2), .width(4)) multiplexer_1 (
    .in0(A), .in1({A[2:0], 1'b0}), .in2({A[1:0], 2'b00}), .in3({A[0], 3'b000}), .out(O), .sel(SHIFT));
endmodule

module ROTATE_RIGHT_SHIFT (
  input  [3:0] A,
  input  [1:0] SHIFT,
  output [3:0] O
);

  Multiplexer #(.select(2), .width(4)) multiplexer_1 (
    .in0(A), .in1({A[0], A[3:1]}), .in2({A[1:0], A[3:2]}), .in3({A[2:0], A[3]}), .out(O), .sel(SHIFT));
endmodule

module ROTATE_LEFT_SHIFT (
  input  [3:0] A,
  input  [1:0] SHIFT,
  output [3:0] O
);

  Multiplexer #(.select(2), .width(4)) multiplexer_1 (
    .in0(A), .in1({A[2:0], A[3]}), .in2({A[1:0], A[3:2]}), .in3({A[0], A[3:1]}), .out(O), .sel(SHIFT));
endmodule

module SHIFT_RIGHT_ARTHMETRIC (
  input  [3:0] A,
  input  [1:0] SHIFT,
  output [3:0] O
);

  Multiplexer #(.select(2), .width(4)) multiplexer_1 (
    .in0(A), .in1({{2{A[3]}}, A[2:1]}), .in2({A[3], 1'b0, A[3:2]}), .in3({A[3], 2'b00, A[3]}), .out(O),
    .sel(SHIFT));
endmodule

module EIGHT_BIT_DIVISION (
  input  [7:0] A,
  input  [7:0] B,
  output [7:0] Remainder,
  output [7:0] Quotient
);

  wire [7:0] division_helper_1_aa, division_helper_1_d, division_helper_2_aa, division_helper_2_d,
       division_helper_3_aa, division_helper_3_d, division_helper_4_aa, division_helper_4_d,
       division_helper_5_aa, division_helper_5_d, division_helper_6_aa, division_helper_6_d,
       division_helper_7_aa, division_helper_7_d, division_helper_8_aa, division_helper_8_d,
       multiplexer_1_out, multiplexer_2_out, multiplexer_3_out, multiplexer_4_out, multiplexer_5_out,
       multiplexer_7_out;
  wire [7:1] multiplexer_6_out_2;
  wire [7:7] multiplexer_6_out;

  Multiplexer #(.width(8)) multiplexer_1 (
    .in0(division_helper_1_aa), .in1(division_helper_1_d), .out(multiplexer_1_out), .sel(Quotient[7]));
  DIVISION_HELPER division_helper_1 (
    .A({{7{1'b0}}, A[7]}), .B(B), .D(division_helper_1_d), .COUT(Quotient[7]), .AA(division_helper_1_aa));
  Multiplexer #(.width(8)) multiplexer_2 (
    .in0(division_helper_2_aa), .in1(division_helper_2_d), .out(multiplexer_2_out), .sel(Quotient[6]));
  DIVISION_HELPER division_helper_2 (
    .A({multiplexer_1_out[6:0], A[6]}), .B(B), .D(division_helper_2_d), .COUT(Quotient[6]),
    .AA(division_helper_2_aa));
  Multiplexer #(.width(8)) multiplexer_3 (
    .in0(division_helper_3_aa), .in1(division_helper_3_d), .out(multiplexer_3_out), .sel(Quotient[5]));
  DIVISION_HELPER division_helper_3 (
    .A({multiplexer_2_out[6:0], A[5]}), .B(B), .D(division_helper_3_d), .COUT(Quotient[5]),
    .AA(division_helper_3_aa));
  Multiplexer #(.width(8)) multiplexer_4 (
    .in0(division_helper_4_aa), .in1(division_helper_4_d), .out(multiplexer_4_out), .sel(Quotient[4]));
  DIVISION_HELPER division_helper_4 (
    .A({multiplexer_3_out[6:0], A[4]}), .B(B), .D(division_helper_4_d), .COUT(Quotient[4]),
    .AA(division_helper_4_aa));
  DIVISION_HELPER division_helper_5 (
    .A({multiplexer_4_out[6:0], A[3]}), .B(B), .D(division_helper_5_d), .COUT(Quotient[3]),
    .AA(division_helper_5_aa));
  Multiplexer #(.width(8)) multiplexer_5 (
    .in0(division_helper_5_aa), .in1(division_helper_5_d), .out(multiplexer_5_out), .sel(Quotient[3]));
  DIVISION_HELPER division_helper_6 (
    .A({multiplexer_5_out[6:0], A[2]}), .B(B), .D(division_helper_6_d), .COUT(Quotient[2]),
    .AA(division_helper_6_aa));
  Multiplexer #(.width(8)) multiplexer_6 (
    .in0(division_helper_6_aa), .in1(division_helper_6_d), .out({multiplexer_6_out[7], multiplexer_6_out_2}),
    .sel(Quotient[2]));
  Multiplexer #(.width(8)) multiplexer_7 (
    .in0(division_helper_7_aa), .in1(division_helper_7_d), .out(multiplexer_7_out), .sel(Quotient[1]));
  DIVISION_HELPER division_helper_7 (
    .A({multiplexer_6_out_2, A[1]}), .B(B), .D(division_helper_7_d), .COUT(Quotient[1]),
    .AA(division_helper_7_aa));
  Multiplexer #(.width(8)) multiplexer_8 (
    .in0(division_helper_8_aa), .in1(division_helper_8_d), .out(Remainder), .sel(Quotient[0]));
  DIVISION_HELPER division_helper_8 (
    .A({multiplexer_7_out[6:0], A[0]}), .B(B), .D(division_helper_8_d), .COUT(Quotient[0]),
    .AA(division_helper_8_aa));
endmodule

module DIVISION_HELPER (
  input  [7:0] B,
  input  [7:0] A,
  output [7:0] D,
  output COUT,
  output [7:0] AA
);

  wire subtractor_1_bout;

  Subtractor subtractor_1 (.a(A), .b(B), .out(D), .bout(subtractor_1_bout));  // open: bin
  not not_1 (COUT, subtractor_1_bout);

  assign AA = A;
endmodule

module EIGHT_BIT_COMPARATOR (
  input  [7:0] B,
  input  [7:0] A,
  output Greater,
  output Greater_OR_Equal,
  output Equal,
  output Less_OR_Equal,
  output Less
);

  wire and_1_out, and_2_out, and_3_out, and_4_out, and_5_out, and_6_out, and_7_out, and_8_out, and_9_out,
       and_10_out, and_11_out, and_12_out, and_13_out, and_14_out, and_15_out, and_16_out,
       comparator_helper_1_a_greater, comparator_helper_1_b_greater, comparator_helper_2_a_greater,
       comparator_helper_2_b_greater, comparator_helper_3_a_greater, comparator_helper_3_b_greater,
       comparator_helper_4_a_greater, comparator_helper_4_b_greater, comparator_helper_5_a_greater,
       comparator_helper_5_b_greater, comparator_helper_6_a_greater, comparator_helper_6_b_greater,
       not_1_out, not_2_out, not_3_out, not_4_out, not_5_out, not_6_out, not_7_out, not_8_out, not_9_out,
       not_10_out, not_11_out, not_12_out, not_13_out, not_14_out, not_15_out, not_16_out;

  not not_1 (not_1_out, B[7]);
  not not_2 (not_2_out, A[7]);
  not not_3 (not_3_out, B[6]);
  not not_4 (not_4_out, A[6]);
  not not_5 (not_5_out, B[5]);
  not not_6 (not_6_out, A[5]);
  not not_7 (not_7_out, B[4]);
  not not_8 (not_8_out, A[4]);
  not not_9 (not_9_out, B[3]);
  not not_10 (not_10_out, A[3]);
  not not_11 (not_11_out, B[2]);
  not not_12 (not_12_out, A[2]);
  not not_13 (not_13_out, B[1]);
  not not_14 (not_14_out, A[1]);
  not not_15 (not_15_out, B[0]);
  not not_16 (not_16_out, A[0]);
  and and_1 (and_1_out, not_1_out, A[7]);
  and and_2 (and_2_out, B[7], not_2_out);
  and and_3 (and_3_out, not_3_out, A[6]);
  and and_4 (and_4_out, B[6], not_4_out);
  and and_5 (and_5_out, not_5_out, A[5]);
  and and_6 (and_6_out, B[5], not_6_out);
  and and_7 (and_7_out, not_7_out, A[4]);
  and and_8 (and_8_out, B[4], not_8_out);
  and and_9 (and_9_out, not_9_out, A[3]);
  and and_10 (and_10_out, B[3], not_10_out);
  and and_11 (and_11_out, not_11_out, A[2]);
  and and_12 (and_12_out, B[2], not_12_out);
  and and_13 (and_13_out, not_13_out, A[1]);
  and and_14 (and_14_out, B[1], not_14_out);
  and and_15 (and_15_out, not_15_out, A[0]);
  and and_16 (and_16_out, B[0], not_16_out);
  COMPARATOR_HELPER comparator_helper_1 (
    .A_G(and_1_out), .B_G(and_2_out), .A_GG(and_3_out), .B_GG(and_4_out),
    .A_GREATER(comparator_helper_1_a_greater), .B_GREATER(comparator_helper_1_b_greater));
  COMPARATOR_HELPER comparator_helper_2 (
    .A_G(and_5_out), .B_G(and_6_out), .A_GG(and_7_out), .B_GG(and_8_out),
    .A_GREATER(comparator_helper_2_a_greater), .B_GREATER(comparator_helper_2_b_greater));
  COMPARATOR_HELPER comparator_helper_3 (
    .A_G(and_9_out), .B_G(and_10_out), .A_GG(and_11_out), .B_GG(and_12_out),
    .A_GREATER(comparator_helper_3_a_greater), .B_GREATER(comparator_helper_3_b_greater));
  COMPARATOR_HELPER comparator_helper_4 (
    .A_G(and_13_out), .B_G(and_14_out), .A_GG(and_15_out), .B_GG(and_16_out),
    .A_GREATER(comparator_helper_4_a_greater), .B_GREATER(comparator_helper_4_b_greater));
  COMPARATOR_HELPER comparator_helper_5 (
    .A_G(comparator_helper_1_a_greater), .B_G(comparator_helper_1_b_greater),
    .A_GG(comparator_helper_2_a_greater), .B_GG(comparator_helper_2_b_greater),
    .A_GREATER(comparator_helper_5_a_greater), .B_GREATER(comparator_helper_5_b_greater));
  COMPARATOR_HELPER comparator_helper_6 (
    .A_G(comparator_helper_3_a_greater), .B_G(comparator_helper_3_b_greater),
    .A_GG(comparator_helper_4_a_greater), .B_GG(comparator_helper_4_b_greater),
    .A_GREATER(comparator_helper_6_a_greater), .B_GREATER(comparator_helper_6_b_greater));
  COMPARATOR_HELPER comparator_helper_7 (
    .A_G(comparator_helper_5_a_greater), .B_G(comparator_helper_5_b_greater),
    .A_GG(comparator_helper_6_a_greater), .B_GG(comparator_helper_6_b_greater), .A_GREATER(Greater),
    .B_GREATER(Less));
  nand nand_1 (Equal, Greater, Less);
  or or_1 (Greater_OR_Equal, Greater, Equal);
  or or_2 (Less_OR_Equal, Equal, Less);
endmodule

module COMPARATOR_HELPER (
  input  A_G,
  input  B_G,
  input  A_GG,
  input  B_GG,
  output A_GREATER,
  output B_GREATER
);

  wire and_1_out, and_2_out, and_3_out, and_4_out, and_5_out, not_1_out, not_2_out, not_3_out, not_4_out;

  not not_1 (not_1_out, A_G);
  not not_2 (not_2_out, B_G);
  not not_3 (not_3_out, A_GG);
  not not_4 (not_4_out, B_GG);
  and and_1 (and_1_out, A_GG, not_4_out);
  and and_2 (and_2_out, A_G, not_2_out);
  and and_3 (and_3_out, not_1_out, not_3_out, B_GG);
  and and_4 (and_4_out, not_1_out, B_G);
  and and_5 (and_5_out, B_G, not_3_out, B_GG);
  or or_1 (A_GREATER, and_1_out, and_2_out);
  or or_2 (B_GREATER, and_3_out, and_4_out, and_5_out);
endmodule

module EIGHT_BIT_REGISTER (
  input  Clock,
  input  Enable,
  input  [7:0] Data,
  output [7:0] O
);

  wire and_1_out;

  and and_1 (and_1_out, Clock, Enable);
  D_Flip_Flop d_ff_1 (.clk(and_1_out), .D(Data[0]), .Q(O[0]));  // open: Qn, preset, reset
  D_Flip_Flop d_ff_2 (.clk(and_1_out), .D(Data[1]), .Q(O[1]));  // open: Qn, preset, reset
  D_Flip_Flop d_ff_3 (.clk(and_1_out), .D(Data[2]), .Q(O[2]));  // open: Qn, preset, reset
  D_Flip_Flop d_ff_4 (.clk(and_1_out), .D(Data[3]), .Q(O[3]));  // open: Qn, preset, reset
  D_Flip_Flop d_ff_5 (.clk(and_1_out), .D(Data[4]), .Q(O[4]));  // open: Qn, preset, reset
  D_Flip_Flop d_ff_6 (.clk(and_1_out), .D(Data[5]), .Q(O[5]));  // open: Qn, preset, reset
  D_Flip_Flop d_ff_7 (.clk(and_1_out), .D(Data[6]), .Q(O[6]));  // open: Qn, preset, reset
  D_Flip_Flop d_ff_8 (.clk(and_1_out), .D(Data[7]), .Q(O[7]));  // open: Qn, preset, reset
endmodule

module SIXTEENxEIGHT_REGISTER (
  input  [3:0] Address,
  input  [7:0] Data,
  input  Enable,
  input  Clock,
  output [7:0] Outputs
);

  wire demultiplexer_1_out0, demultiplexer_1_out1, demultiplexer_1_out2, demultiplexer_1_out3,
       demultiplexer_1_out4, demultiplexer_1_out5, demultiplexer_1_out6, demultiplexer_1_out7,
       demultiplexer_1_out8, demultiplexer_1_out9, demultiplexer_1_out10, demultiplexer_1_out11,
       demultiplexer_1_out12, demultiplexer_1_out13, demultiplexer_1_out14, demultiplexer_1_out15;
  wire [7:0] eight_bit_register_1_o, eight_bit_register_2_o, eight_bit_register_3_o, eight_bit_register_4_o,
       eight_bit_register_5_o, eight_bit_register_6_o, eight_bit_register_7_o, eight_bit_register_8_o,
       eight_bit_register_9_o, eight_bit_register_10_o, eight_bit_register_11_o, eight_bit_register_12_o,
       eight_bit_register_13_o, eight_bit_register_14_o, eight_bit_register_15_o, eight_bit_register_16_o;

  Demultiplexer #(.select(4)) demultiplexer_1 (
    .out0(demultiplexer_1_out0), .out1(demultiplexer_1_out1), .out2(demultiplexer_1_out2),
    .out3(demultiplexer_1_out3), .out4(demultiplexer_1_out4), .out5(demultiplexer_1_out5),
    .out6(demultiplexer_1_out6), .out7(demultiplexer_1_out7), .out8(demultiplexer_1_out8),
    .out9(demultiplexer_1_out9), .out10(demultiplexer_1_out10), .out11(demultiplexer_1_out11),
    .out12(demultiplexer_1_out12), .out13(demultiplexer_1_out13), .out14(demultiplexer_1_out14),
    .out15(demultiplexer_1_out15), .in(Enable), .sel(Address));
  EIGHT_BIT_REGISTER eight_bit_register_1 (
    .Clock(Clock), .Enable(demultiplexer_1_out0), .Data(Data), .O(eight_bit_register_1_o));
  EIGHT_BIT_REGISTER eight_bit_register_2 (
    .Clock(Clock), .Enable(demultiplexer_1_out1), .Data(Data), .O(eight_bit_register_2_o));
  EIGHT_BIT_REGISTER eight_bit_register_3 (
    .Clock(Clock), .Enable(demultiplexer_1_out2), .Data(Data), .O(eight_bit_register_3_o));
  EIGHT_BIT_REGISTER eight_bit_register_4 (
    .Clock(Clock), .Enable(demultiplexer_1_out3), .Data(Data), .O(eight_bit_register_4_o));
  EIGHT_BIT_REGISTER eight_bit_register_5 (
    .Clock(Clock), .Enable(demultiplexer_1_out4), .Data(Data), .O(eight_bit_register_5_o));
  EIGHT_BIT_REGISTER eight_bit_register_6 (
    .Clock(Clock), .Enable(demultiplexer_1_out5), .Data(Data), .O(eight_bit_register_6_o));
  EIGHT_BIT_REGISTER eight_bit_register_7 (
    .Clock(Clock), .Enable(demultiplexer_1_out6), .Data(Data), .O(eight_bit_register_7_o));
  EIGHT_BIT_REGISTER eight_bit_register_8 (
    .Clock(Clock), .Enable(demultiplexer_1_out7), .Data(Data), .O(eight_bit_register_8_o));
  EIGHT_BIT_REGISTER eight_bit_register_9 (
    .Clock(Clock), .Enable(demultiplexer_1_out8), .Data(Data), .O(eight_bit_register_9_o));
  EIGHT_BIT_REGISTER eight_bit_register_10 (
    .Clock(Clock), .Enable(demultiplexer_1_out9), .Data(Data), .O(eight_bit_register_10_o));
  EIGHT_BIT_REGISTER eight_bit_register_11 (
    .Clock(Clock), .Enable(demultiplexer_1_out10), .Data(Data), .O(eight_bit_register_11_o));
  EIGHT_BIT_REGISTER eight_bit_register_12 (
    .Clock(Clock), .Enable(demultiplexer_1_out11), .Data(Data), .O(eight_bit_register_12_o));
  EIGHT_BIT_REGISTER eight_bit_register_13 (
    .Clock(Clock), .Enable(demultiplexer_1_out12), .Data(Data), .O(eight_bit_register_13_o));
  EIGHT_BIT_REGISTER eight_bit_register_14 (
    .Clock(Clock), .Enable(demultiplexer_1_out13), .Data(Data), .O(eight_bit_register_14_o));
  EIGHT_BIT_REGISTER eight_bit_register_15 (
    .Clock(Clock), .Enable(demultiplexer_1_out14), .Data(Data), .O(eight_bit_register_15_o));
  EIGHT_BIT_REGISTER eight_bit_register_16 (
    .Clock(Clock), .Enable(demultiplexer_1_out15), .Data(Data), .O(eight_bit_register_16_o));
  Multiplexer #(.select(4), .width(8)) multiplexer_1 (
    .in0(eight_bit_register_1_o), .in1(eight_bit_register_2_o), .in2(eight_bit_register_3_o),
    .in3(eight_bit_register_4_o), .in4(eight_bit_register_5_o), .in5(eight_bit_register_6_o),
    .in6(eight_bit_register_7_o), .in7(eight_bit_register_8_o), .in8(eight_bit_register_9_o),
    .in9(eight_bit_register_10_o), .in10(eight_bit_register_11_o), .in11(eight_bit_register_12_o),
    .in12(eight_bit_register_13_o), .in13(eight_bit_register_14_o), .in14(eight_bit_register_15_o),
    .in15(eight_bit_register_16_o), .out(Outputs), .sel(Address));
endmodule

module TWOFIFTYSIXxEIGHT_REGISTER (
  input  [7:0] Address,
  input  [7:0] Data,
  input  ENABLE_READ,
  input  ENABLE_WRITE,
  input  CLOCK,
  output [7:0] Outputs
);

  wire and_1_out, demultiplexer_1_out0, demultiplexer_1_out1, demultiplexer_1_out2, demultiplexer_1_out3,
       demultiplexer_1_out4, demultiplexer_1_out5, demultiplexer_1_out6, demultiplexer_1_out7,
       demultiplexer_1_out8, demultiplexer_1_out9, demultiplexer_1_out10, demultiplexer_1_out11,
       demultiplexer_1_out12, demultiplexer_1_out13, demultiplexer_1_out14, demultiplexer_1_out15;
  wire [7:0] multiplexer_1_out, sixteenxeight_register_1_outputs, sixteenxeight_register_2_outputs,
       sixteenxeight_register_3_outputs, sixteenxeight_register_4_outputs, sixteenxeight_register_5_outputs,
       sixteenxeight_register_6_outputs, sixteenxeight_register_7_outputs, sixteenxeight_register_8_outputs,
       sixteenxeight_register_9_outputs, sixteenxeight_register_10_outputs,
       sixteenxeight_register_11_outputs, sixteenxeight_register_12_outputs,
       sixteenxeight_register_13_outputs, sixteenxeight_register_14_outputs,
       sixteenxeight_register_15_outputs, sixteenxeight_register_16_outputs;

  and and_1 (and_1_out, ENABLE_WRITE, ENABLE_READ);
  Demultiplexer #(.select(4)) demultiplexer_1 (
    .out0(demultiplexer_1_out0), .out1(demultiplexer_1_out1), .out2(demultiplexer_1_out2),
    .out3(demultiplexer_1_out3), .out4(demultiplexer_1_out4), .out5(demultiplexer_1_out5),
    .out6(demultiplexer_1_out6), .out7(demultiplexer_1_out7), .out8(demultiplexer_1_out8),
    .out9(demultiplexer_1_out9), .out10(demultiplexer_1_out10), .out11(demultiplexer_1_out11),
    .out12(demultiplexer_1_out12), .out13(demultiplexer_1_out13), .out14(demultiplexer_1_out14),
    .out15(demultiplexer_1_out15), .in(and_1_out), .sel(Address[7:4]));
  SIXTEENxEIGHT_REGISTER sixteenxeight_register_1 (
    .Address(Address[3:0]), .Data(Data), .Enable(demultiplexer_1_out0), .Clock(CLOCK),
    .Outputs(sixteenxeight_register_1_outputs));
  SIXTEENxEIGHT_REGISTER sixteenxeight_register_2 (
    .Address(Address[3:0]), .Data(Data), .Enable(demultiplexer_1_out1), .Clock(CLOCK),
    .Outputs(sixteenxeight_register_2_outputs));
  SIXTEENxEIGHT_REGISTER sixteenxeight_register_3 (
    .Address(Address[3:0]), .Data(Data), .Enable(demultiplexer_1_out2), .Clock(CLOCK),
    .Outputs(sixteenxeight_register_3_outputs));
  SIXTEENxEIGHT_REGISTER sixteenxeight_register_4 (
    .Address(Address[3:0]), .Data(Data), .Enable(demultiplexer_1_out3), .Clock(CLOCK),
    .Outputs(sixteenxeight_register_4_outputs));
  SIXTEENxEIGHT_REGISTER sixteenxeight_register_5 (
    .Address(Address[3:0]), .Data(Data), .Enable(demultiplexer_1_out4), .Clock(CLOCK),
    .Outputs(sixteenxeight_register_5_outputs));
  SIXTEENxEIGHT_REGISTER sixteenxeight_register_6 (
    .Address(Address[3:0]), .Data(Data), .Enable(demultiplexer_1_out5), .Clock(CLOCK),
    .Outputs(sixteenxeight_register_6_outputs));
  SIXTEENxEIGHT_REGISTER sixteenxeight_register_7 (
    .Address(Address[3:0]), .Data(Data), .Enable(demultiplexer_1_out6), .Clock(CLOCK),
    .Outputs(sixteenxeight_register_7_outputs));
  SIXTEENxEIGHT_REGISTER sixteenxeight_register_8 (
    .Address(Address[3:0]), .Data(Data), .Enable(demultiplexer_1_out7), .Clock(CLOCK),
    .Outputs(sixteenxeight_register_8_outputs));
  SIXTEENxEIGHT_REGISTER sixteenxeight_register_9 (
    .Address(Address[3:0]), .Data(Data), .Enable(demultiplexer_1_out8), .Clock(CLOCK),
    .Outputs(sixteenxeight_register_9_outputs));
  SIXTEENxEIGHT_REGISTER sixteenxeight_register_10 (
    .Address(Address[3:0]), .Data(Data), .Enable(demultiplexer_1_out9), .Clock(CLOCK),
    .Outputs(sixteenxeight_register_10_outputs));
  SIXTEENxEIGHT_REGISTER sixteenxeight_register_11 (
    .Address(Address[3:0]), .Data(Data), .Enable(demultiplexer_1_out10), .Clock(CLOCK),
    .Outputs(sixteenxeight_register_11_outputs));
  SIXTEENxEIGHT_REGISTER sixteenxeight_register_12 (
    .Address(Address[3:0]), .Data(Data), .Enable(demultiplexer_1_out11), .Clock(CLOCK),
    .Outputs(sixteenxeight_register_12_outputs));
  SIXTEENxEIGHT_REGISTER sixteenxeight_register_13 (
    .Address(Address[3:0]), .Data(Data), .Enable(demultiplexer_1_out12), .Clock(CLOCK),
    .Outputs(sixteenxeight_register_13_outputs));
  SIXTEENxEIGHT_REGISTER sixteenxeight_register_14 (
    .Address(Address[3:0]), .Data(Data), .Enable(demultiplexer_1_out13), .Clock(CLOCK),
    .Outputs(sixteenxeight_register_14_outputs));
  SIXTEENxEIGHT_REGISTER sixteenxeight_register_15 (
    .Address(Address[3:0]), .Data(Data), .Enable(demultiplexer_1_out14), .Clock(CLOCK),
    .Outputs(sixteenxeight_register_15_outputs));
  SIXTEENxEIGHT_REGISTER sixteenxeight_register_16 (
    .Address(Address[3:0]), .Data(Data), .Enable(demultiplexer_1_out15), .Clock(CLOCK),
    .Outputs(sixteenxeight_register_16_outputs));
  Multiplexer #(.select(4), .width(8)) multiplexer_1 (
    .in0(sixteenxeight_register_1_outputs), .in1(sixteenxeight_register_2_outputs),
    .in2(sixteenxeight_register_3_outputs), .in3(sixteenxeight_register_4_outputs),
    .in4(sixteenxeight_register_5_outputs), .in5(sixteenxeight_register_6_outputs),
    .in6(sixteenxeight_register_7_outputs), .in7(sixteenxeight_register_8_outputs),
    .in8(sixteenxeight_register_9_outputs), .in9(sixteenxeight_register_10_outputs),
    .in10(sixteenxeight_register_11_outputs), .in11(sixteenxeight_register_12_outputs),
    .in12(sixteenxeight_register_13_outputs), .in13(sixteenxeight_register_14_outputs),
    .in14(sixteenxeight_register_15_outputs), .in15(sixteenxeight_register_16_outputs),
    .out(multiplexer_1_out), .sel(Address[7:4]));
  Multiplexer #(.width(8)) multiplexer_2 (.in0({8{1'b0}}), .in1(multiplexer_1_out), .out(Outputs), .sel(ENABLE_READ));
endmodule

module SIXTEEN_BIT_PROGRAM_COUNTER (
  input  CLOCK,
  input  RESET,
  input  WRITE,
  input  [15:0] INP,
  output [15:0] COUNT
);

  wire and_1_out, and_2_out, and_3_out, and_4_out, and_5_out, and_6_out, and_7_out, and_8_out, and_9_out,
       and_10_out, and_11_out, and_12_out, and_13_out, and_14_out, and_15_out, and_16_out, and_17_out,
       and_18_out, and_19_out, and_20_out, and_21_out, and_22_out, and_23_out, and_24_out, and_25_out,
       and_26_out, and_27_out, and_28_out, and_29_out, and_30_out, and_31_out, and_32_out, d_ff_1_qn,
       d_ff_2_qn, d_ff_3_qn, d_ff_4_qn, d_ff_5_qn, d_ff_6_qn, d_ff_7_qn, d_ff_8_qn, d_ff_9_qn, d_ff_10_qn,
       d_ff_11_qn, d_ff_12_qn, d_ff_13_qn, d_ff_14_qn, d_ff_15_qn, d_ff_16_qn, or_1_out, or_2_out, or_3_out,
       or_4_out, or_5_out, or_6_out, or_7_out, or_8_out, or_9_out, or_10_out, or_11_out, or_12_out,
       or_13_out, or_14_out, or_15_out, or_16_out;

  and and_1 (and_1_out, WRITE, INP[0]);
  and and_2 (and_2_out, WRITE, ~INP[0]);  // AND_Gate
  and and_3 (and_3_out, WRITE, INP[1]);
  and and_4 (and_4_out, WRITE, ~INP[1]);  // AND_Gate
  and and_5 (and_5_out, WRITE, INP[2]);
  and and_6 (and_6_out, WRITE, ~INP[2]);  // AND_Gate
  and and_7 (and_7_out, WRITE, INP[3]);
  and and_8 (and_8_out, WRITE, ~INP[3]);  // AND_Gate
  and and_9 (and_9_out, WRITE, INP[4]);
  and and_10 (and_10_out, WRITE, ~INP[4]);  // AND_Gate
  and and_11 (and_11_out, WRITE, INP[5]);
  and and_12 (and_12_out, WRITE, ~INP[5]);  // AND_Gate
  and and_13 (and_13_out, WRITE, INP[6]);
  and and_14 (and_14_out, WRITE, ~INP[6]);  // AND_Gate
  and and_15 (and_15_out, WRITE, INP[7]);
  and and_16 (and_16_out, WRITE, ~INP[7]);  // AND_Gate
  and and_17 (and_17_out, WRITE, INP[8]);
  and and_18 (and_18_out, WRITE, ~INP[8]);  // AND_Gate
  and and_19 (and_19_out, WRITE, INP[9]);
  and and_20 (and_20_out, WRITE, ~INP[9]);  // AND_Gate
  and and_21 (and_21_out, WRITE, INP[10]);
  and and_22 (and_22_out, WRITE, ~INP[10]);  // AND_Gate
  and and_23 (and_23_out, WRITE, INP[11]);
  and and_24 (and_24_out, WRITE, ~INP[11]);  // AND_Gate
  and and_25 (and_25_out, WRITE, INP[12]);
  and and_26 (and_26_out, WRITE, ~INP[12]);  // AND_Gate
  and and_27 (and_27_out, WRITE, INP[13]);
  and and_28 (and_28_out, WRITE, ~INP[13]);  // AND_Gate
  and and_29 (and_29_out, WRITE, INP[14]);
  and and_30 (and_30_out, WRITE, ~INP[14]);  // AND_Gate
  and and_31 (and_31_out, WRITE, INP[15]);
  and and_32 (and_32_out, WRITE, ~INP[15]);  // AND_Gate
  D_Flip_Flop d_ff_1 (.D(d_ff_1_qn), .clk(CLOCK), .Q(COUNT[0]), .Qn(d_ff_1_qn), .preset(and_1_out), .reset(or_1_out));
  or or_1 (or_1_out, RESET, and_2_out);
  or or_2 (or_2_out, RESET, and_4_out);
  or or_3 (or_3_out, RESET, and_6_out);
  or or_4 (or_4_out, RESET, and_8_out);
  or or_5 (or_5_out, RESET, and_10_out);
  or or_6 (or_6_out, RESET, and_12_out);
  or or_7 (or_7_out, RESET, and_14_out);
  or or_8 (or_8_out, RESET, and_16_out);
  or or_9 (or_9_out, RESET, and_18_out);
  or or_10 (or_10_out, RESET, and_20_out);
  or or_11 (or_11_out, RESET, and_22_out);
  or or_12 (or_12_out, RESET, and_24_out);
  or or_13 (or_13_out, RESET, and_26_out);
  or or_14 (or_14_out, RESET, and_28_out);
  or or_15 (or_15_out, RESET, and_30_out);
  or or_16 (or_16_out, RESET, and_32_out);
  D_Flip_Flop d_ff_2 (
    .D(d_ff_2_qn), .clk(d_ff_1_qn), .Q(COUNT[1]), .Qn(d_ff_2_qn), .preset(and_3_out), .reset(or_2_out));
  D_Flip_Flop d_ff_3 (
    .D(d_ff_3_qn), .clk(d_ff_2_qn), .Q(COUNT[2]), .Qn(d_ff_3_qn), .preset(and_5_out), .reset(or_3_out));
  D_Flip_Flop d_ff_4 (
    .D(d_ff_4_qn), .clk(d_ff_3_qn), .Q(COUNT[3]), .Qn(d_ff_4_qn), .preset(and_7_out), .reset(or_4_out));
  D_Flip_Flop d_ff_5 (
    .D(d_ff_5_qn), .clk(d_ff_4_qn), .Q(COUNT[4]), .Qn(d_ff_5_qn), .preset(and_9_out), .reset(or_5_out));
  D_Flip_Flop d_ff_6 (
    .D(d_ff_6_qn), .clk(d_ff_5_qn), .Q(COUNT[5]), .Qn(d_ff_6_qn), .preset(and_11_out), .reset(or_6_out));
  D_Flip_Flop d_ff_7 (
    .D(d_ff_7_qn), .clk(d_ff_6_qn), .Q(COUNT[6]), .Qn(d_ff_7_qn), .preset(and_13_out), .reset(or_7_out));
  D_Flip_Flop d_ff_8 (
    .D(d_ff_8_qn), .clk(d_ff_7_qn), .Q(COUNT[7]), .Qn(d_ff_8_qn), .preset(and_15_out), .reset(or_8_out));
  D_Flip_Flop d_ff_9 (
    .D(d_ff_9_qn), .clk(d_ff_8_qn), .Q(COUNT[8]), .Qn(d_ff_9_qn), .preset(and_17_out), .reset(or_9_out));
  D_Flip_Flop d_ff_10 (
    .D(d_ff_10_qn), .clk(d_ff_9_qn), .Q(COUNT[9]), .Qn(d_ff_10_qn), .preset(and_19_out), .reset(or_10_out));
  D_Flip_Flop d_ff_11 (
    .D(d_ff_11_qn), .clk(d_ff_10_qn), .Q(COUNT[10]), .Qn(d_ff_11_qn), .preset(and_21_out), .reset(or_11_out));
  D_Flip_Flop d_ff_12 (
    .D(d_ff_12_qn), .clk(d_ff_11_qn), .Q(COUNT[11]), .Qn(d_ff_12_qn), .preset(and_23_out), .reset(or_12_out));
  D_Flip_Flop d_ff_13 (
    .D(d_ff_13_qn), .clk(d_ff_12_qn), .Q(COUNT[12]), .Qn(d_ff_13_qn), .preset(and_25_out), .reset(or_13_out));
  D_Flip_Flop d_ff_14 (
    .D(d_ff_14_qn), .clk(d_ff_13_qn), .Q(COUNT[13]), .Qn(d_ff_14_qn), .preset(and_27_out), .reset(or_14_out));
  D_Flip_Flop d_ff_15 (
    .D(d_ff_15_qn), .clk(d_ff_14_qn), .Q(COUNT[14]), .Qn(d_ff_15_qn), .preset(and_29_out), .reset(or_15_out));
  D_Flip_Flop d_ff_16 (
    .D(d_ff_16_qn), .clk(d_ff_15_qn), .Q(COUNT[15]), .Qn(d_ff_16_qn), .preset(and_31_out), .reset(or_16_out));
  Register #(.width(16)) register_1 (.D(COUNT), .en(CLOCK), .clk(CLOCK));  // open: Q, clr
endmodule

module TWO_BIT_CLOCK (
  input  CLOCK,
  input  RESET,
  output OUT1,
  output OUT2
);

  wire d_ff_1_qn, d_ff_2_q, not_1_out;

  D_Flip_Flop d_ff_1 (.D(d_ff_1_qn), .clk(CLOCK), .Q(OUT1), .Qn(d_ff_1_qn), .reset(RESET));  // open: preset
  not not_1 (not_1_out, CLOCK);
  D_Flip_Flop d_ff_2 (.D(OUT1), .clk(not_1_out), .Q(d_ff_2_q), .reset(RESET));  // open: Qn, preset
  and and_1 (OUT2, d_ff_2_q, d_ff_1_qn);
endmodule

module SIXTEEN_EIGHT_REGISTER (
  input  RESET,
  input  [3:0] WRITE_Address,
  input  [7:0] INPUT_Data,
  input  ENABLE,
  input  CLOCK,
  input  [3:0] INPUT_ADDRESS_A,
  input  [3:0] INPUT_ADDRESS_B,
  output [7:0] R0,
  output [7:0] R1,
  output [7:0] R2,
  output [7:0] R3,
  output [7:0] F4,
  output [7:0] F5,
  output [7:0] OUTPUT_A,
  output [7:0] F6,
  output [7:0] OUTPUT_B,
  output [7:0] R7,
  output [7:0] R8,
  output [7:0] R9,
  output [7:0] R10,
  output [7:0] R11,
  output [7:0] R12,
  output [7:0] R13,
  output [7:0] R14,
  output [7:0] R15
);

  wire and_1_out, demultiplexer_1_out0, demultiplexer_1_out1, demultiplexer_1_out2, demultiplexer_1_out3,
       demultiplexer_1_out4, demultiplexer_1_out5, demultiplexer_1_out6, demultiplexer_1_out7,
       demultiplexer_1_out8, demultiplexer_1_out9, demultiplexer_1_out10, demultiplexer_1_out11,
       demultiplexer_1_out12, demultiplexer_1_out13, demultiplexer_1_out14, demultiplexer_1_out15;

  and and_1 (and_1_out, CLOCK, ENABLE);
  Demultiplexer #(.select(4)) demultiplexer_1 (
    .out0(demultiplexer_1_out0), .out1(demultiplexer_1_out1), .out2(demultiplexer_1_out2),
    .out3(demultiplexer_1_out3), .out4(demultiplexer_1_out4), .out5(demultiplexer_1_out5),
    .out6(demultiplexer_1_out6), .out7(demultiplexer_1_out7), .out8(demultiplexer_1_out8),
    .out9(demultiplexer_1_out9), .out10(demultiplexer_1_out10), .out11(demultiplexer_1_out11),
    .out12(demultiplexer_1_out12), .out13(demultiplexer_1_out13), .out14(demultiplexer_1_out14),
    .out15(demultiplexer_1_out15), .in(and_1_out), .sel(WRITE_Address));
  Register register_1 (.D(INPUT_Data), .en(demultiplexer_1_out0), .clk(demultiplexer_1_out0), .Q(R0), .clr(RESET));
  Register register_2 (.D(INPUT_Data), .en(demultiplexer_1_out1), .clk(demultiplexer_1_out1), .Q(R1), .clr(RESET));
  Register register_3 (.D(INPUT_Data), .en(demultiplexer_1_out2), .clk(demultiplexer_1_out2), .Q(R2), .clr(RESET));
  Register register_4 (.D(INPUT_Data), .en(demultiplexer_1_out3), .clk(demultiplexer_1_out3), .Q(R3), .clr(RESET));
  Register register_5 (.D(INPUT_Data), .en(demultiplexer_1_out4), .clk(demultiplexer_1_out4), .Q(F4), .clr(RESET));
  Register register_6 (.D(INPUT_Data), .en(demultiplexer_1_out5), .clk(demultiplexer_1_out5), .Q(F5), .clr(RESET));
  Register register_7 (.D(INPUT_Data), .en(demultiplexer_1_out6), .clk(demultiplexer_1_out6), .Q(F6), .clr(RESET));
  Register register_8 (.D(INPUT_Data), .en(demultiplexer_1_out7), .clk(demultiplexer_1_out7), .Q(R7), .clr(RESET));
  Register register_9 (.D(INPUT_Data), .en(demultiplexer_1_out8), .clk(demultiplexer_1_out8), .Q(R8), .clr(RESET));
  Register register_10 (.D(INPUT_Data), .en(demultiplexer_1_out9), .clk(demultiplexer_1_out9), .Q(R9), .clr(RESET));
  Register register_11 (.D(INPUT_Data), .en(demultiplexer_1_out10), .clk(demultiplexer_1_out10), .Q(R10), .clr(RESET));
  Register register_12 (.D(INPUT_Data), .en(demultiplexer_1_out11), .clk(demultiplexer_1_out11), .Q(R11), .clr(RESET));
  Register register_13 (.D(INPUT_Data), .en(demultiplexer_1_out12), .clk(demultiplexer_1_out12), .Q(R12), .clr(RESET));
  Register register_14 (.D(INPUT_Data), .en(demultiplexer_1_out13), .clk(demultiplexer_1_out13), .Q(R13), .clr(RESET));
  Register register_15 (.D(INPUT_Data), .en(demultiplexer_1_out14), .clk(demultiplexer_1_out14), .Q(R14), .clr(RESET));
  Register register_16 (.D(INPUT_Data), .en(demultiplexer_1_out15), .clk(demultiplexer_1_out15), .Q(R15), .clr(RESET));
  Multiplexer #(.select(4), .width(8)) multiplexer_1 (
    .in0(R0), .in1(R1), .in2(R2), .in3(R3), .in4(F4), .in5(F5), .in6(F6), .in7(R7), .in8(R8), .in9(R9),
    .in10(R10), .in11(R11), .in12(R12), .in13(R13), .in14(R14), .in15(R15), .out(OUTPUT_A),
    .sel(INPUT_ADDRESS_A));
  Multiplexer #(.select(4), .width(8)) multiplexer_2 (
    .in0(R0), .in1(R1), .in2(R2), .in3(R3), .in4(F4), .in5(F5), .in6(F6), .in7(R7), .in8(R8), .in9(R9),
    .in10(R10), .in11(R11), .in12(R12), .in13(R13), .in14(R14), .in15(R15), .out(OUTPUT_B),
    .sel(INPUT_ADDRESS_B));
endmodule

module INC_DEC_FOUR_BIT_COUNTER (
  input  clk,
  input  shf,
  output [3:0] OUTPUTS,
  output BORROW,
  output CARRY
);

  wire and_3_out, and_4_out, and_5_out, and_6_out, and_7_out, and_8_out, and_9_out, and_10_out, and_11_out,
       and_12_out, and_13_out, and_14_out, and_15_out, and_16_out, and_17_out, and_18_out, and_19_out,
       and_20_out, and_21_out, and_22_out, not_1_out, not_2_out, not_3_out, not_4_out, not_5_out, not_6_out,
       or_1_out, or_2_out, or_3_out, or_4_out;
  wire [3:0] register_1_q;

  Register #(.width(4)) register_1 (.D(OUTPUTS), .clk(clk), .Q(register_1_q));  // open: en, clr
  D_Flip_Flop d_ff_1 (.D(or_1_out), .clk(clk), .Q(OUTPUTS[3]));  // open: Qn, preset, reset
  D_Flip_Flop d_ff_2 (.D(or_2_out), .clk(clk), .Q(OUTPUTS[2]));  // open: Qn, preset, reset
  D_Flip_Flop d_ff_3 (.D(or_3_out), .clk(clk), .Q(OUTPUTS[1]));  // open: Qn, preset, reset
  D_Flip_Flop d_ff_4 (.D(or_4_out), .clk(clk), .Q(OUTPUTS[0]));  // open: Qn, preset, reset
  and and_1 (BORROW, ~OUTPUTS[0], ~OUTPUTS[1], ~OUTPUTS[2], ~OUTPUTS[3], register_1_q[0], register_1_q[1], register_1_q[2], register_1_q[3]);  // AND_Gate
  and and_2 (CARRY, OUTPUTS[0], OUTPUTS[1], OUTPUTS[2], OUTPUTS[3], ~register_1_q[0], ~register_1_q[1], ~register_1_q[2], ~register_1_q[3]);  // AND_Gate
  not not_1 (not_1_out, OUTPUTS[3]);
  not not_2 (not_2_out, OUTPUTS[2]);
  not not_3 (not_3_out, OUTPUTS[1]);
  not not_4 (not_4_out, OUTPUTS[0]);
  not not_5 (not_5_out, 1'b1);
  not not_6 (not_6_out, shf);
  and and_3 (and_3_out, not_1_out, not_2_out, not_3_out, not_4_out, 1'b1, shf);
  and and_4 (and_4_out, not_1_out, OUTPUTS[2], OUTPUTS[1], OUTPUTS[0], 1'b1, not_6_out);
  and and_5 (and_5_out, OUTPUTS[3], not_5_out);
  and and_6 (and_6_out, OUTPUTS[3], OUTPUTS[2], not_3_out);
  and and_7 (and_7_out, OUTPUTS[3], not_4_out, not_6_out);
  and and_8 (and_8_out, OUTPUTS[3], not_2_out, OUTPUTS[0]);
  and and_9 (and_9_out, OUTPUTS[3], OUTPUTS[1], shf);
  and and_10 (and_10_out, not_2_out, not_3_out, not_4_out, 1'b1, shf);
  and and_11 (and_11_out, not_2_out, OUTPUTS[1], OUTPUTS[0], 1'b1, not_6_out);
  and and_12 (and_12_out, OUTPUTS[2], not_5_out);
  and and_13 (and_13_out, OUTPUTS[2], not_3_out, OUTPUTS[0]);
  and and_14 (and_14_out, OUTPUTS[2], not_4_out, not_6_out);
  and and_15 (and_15_out, OUTPUTS[2], OUTPUTS[1], shf);
  and and_16 (and_16_out, not_3_out, not_4_out, 1'b1, shf);
  and and_17 (and_17_out, not_3_out, OUTPUTS[0], 1'b1, not_6_out);
  and and_18 (and_18_out, OUTPUTS[1], not_5_out);
  and and_19 (and_19_out, OUTPUTS[1], not_4_out, not_6_out);
  and and_20 (and_20_out, OUTPUTS[1], OUTPUTS[0], shf);
  and and_21 (and_21_out, not_4_out, 1'b1);
  and and_22 (and_22_out, OUTPUTS[0], not_5_out);
  or or_1 (or_1_out, and_3_out, and_4_out, and_5_out, and_6_out, and_7_out, and_8_out, and_9_out);
  or or_2 (or_2_out, and_10_out, and_11_out, and_12_out, and_13_out, and_14_out, and_15_out);
  or or_3 (or_3_out, and_16_out, and_17_out, and_18_out, and_19_out, and_20_out);
  or or_4 (or_4_out, and_21_out, and_22_out);

  // Notes on the sheet:
  //   0x0F
  //   0xF0
endmodule

module INC_DEC_EIGHT_BIT_COUNTER (
  input  CLOCK,
  input  INC_DEC,
  output [7:0] NUM,
  output CARRY,
  output BORROW
);

  wire inc_dec_four_bit_counter_1_borrow, inc_dec_four_bit_counter_1_carry, or_1_out;

  INC_DEC_FOUR_BIT_COUNTER inc_dec_four_bit_counter_1 (
    .clk(CLOCK), .shf(INC_DEC), .BORROW(inc_dec_four_bit_counter_1_borrow),
    .CARRY(inc_dec_four_bit_counter_1_carry), .OUTPUTS(NUM[3:0]));
  or or_1 (or_1_out, inc_dec_four_bit_counter_1_carry, inc_dec_four_bit_counter_1_borrow);
  INC_DEC_FOUR_BIT_COUNTER inc_dec_four_bit_counter_2 (
    .clk(or_1_out), .shf(INC_DEC), .BORROW(BORROW), .CARRY(CARRY), .OUTPUTS(NUM[7:4]));
endmodule

module CONTROL_LOGIC_UNIT (
  input  [7:0] R1_IN,
  input  [7:0] R2_IN,
  input  [7:0] RAM_IN,
  input  [7:0] STACK_IN,
  input  [7:0] INSTRUCTION_BUS,
  input  [15:0] CALL_ADDRESS_IN,
  input  Clock,
  input  RESET,
  output HALT,
  output SAVE_TO_RAM,
  output SAVE_VIDEO,
  output SAVE_REGISTER,
  output RTRN,
  output PUSH,
  output POP,
  output [7:0] RESULT,
  output [7:0] out_17,
  output JUMP,
  output CALL,
  output [15:0] JUMP_ADDRESS,
  output [3:0] REGISTER_DESTINATION,
  output [3:0] REGISTER_1_OUT,
  output [3:0] REGISTER_2_OUT
);

  wire clu_helper_categoriser_1_carry_enable, clu_helper_categoriser_1_compare_flags,
       clu_helper_categoriser_1_cycle_1, clu_helper_categoriser_1_cycle_2, clu_helper_categoriser_1_imm8_reg,
       clu_helper_command_1_carry, clu_helper_command_1_equal_than, clu_helper_command_1_greater_than,
       clu_helper_command_1_less_than, clu_helper_cycle_manager_1_final_cycle,
       clu_helper_cycle_manager_1_first_cycle, clu_helper_cycle_manager_1_second_cycle,
       clu_helper_cycle_manager_1_third_cycle, clu_helper_flag_manager_1_carry_out,
       clu_helper_flag_manager_1_equal_out, clu_helper_flag_manager_1_greater_out,
       clu_helper_flag_manager_1_less_out, clu_helper_flag_manager_1_zero_out, clu_helper_jump_manager_1_jump;
  wire [1:0] clu_helper_categoriser_1_destination_selector;
  wire [7:0] clu_helper_register_manager_1_imm8_1, clu_helper_register_manager_1_imm8_2;
  wire [12:0] clu_helper_categoriser_1_jump_commands;
  wire [15:0] clu_helper_command_1_jump_address;

  CLU_Helper_Cycle_Manager clu_helper_cycle_manager_1 (
    .CLOCK(Clock), .CYCLE_2(clu_helper_categoriser_1_cycle_2), .RESET(RESET),
    .CYCLE_1(clu_helper_categoriser_1_cycle_1), .SECOND_CYCLE(clu_helper_cycle_manager_1_second_cycle),
    .FIRST_CYCLE(clu_helper_cycle_manager_1_first_cycle),
    .THIRD_CYCLE(clu_helper_cycle_manager_1_third_cycle), .FINAL_CYCLE(clu_helper_cycle_manager_1_final_cycle));
  CLU_Helper_Categoriser clu_helper_categoriser_1 (
    .FINAL_CYCLE(clu_helper_cycle_manager_1_final_cycle), .INSTRUCTION(out_17), .RTN(RTRN), .HALT(HALT),
    .JUMP_COMMANDS(clu_helper_categoriser_1_jump_commands), .POP(POP), .PUSH(PUSH),
    .COMPARE_FLAGS(clu_helper_categoriser_1_compare_flags),
    .CARRY_ENABLE(clu_helper_categoriser_1_carry_enable), .SAVE_TO_RAM(SAVE_TO_RAM),
    .CYCLE_1(clu_helper_categoriser_1_cycle_1), .CYCLE_2(clu_helper_categoriser_1_cycle_2),
    .IMM8_REG(clu_helper_categoriser_1_imm8_reg), .SAVE_VIDEO(SAVE_VIDEO),
    .DESTINATION_SELECTOR(clu_helper_categoriser_1_destination_selector), .SAVE_TO_REGISTER(SAVE_REGISTER));  // open: NOP, CYCLE_3
  CLU_Helper_Register_Manager clu_helper_register_manager_1 (
    .INSTRUCTION_BUS(INSTRUCTION_BUS), .THIRD_CYCLE(clu_helper_cycle_manager_1_third_cycle),
    .SECOND_CYCLE(clu_helper_cycle_manager_1_second_cycle), .CLOCK(Clock),
    .FIRST_CYCLE(clu_helper_cycle_manager_1_first_cycle), .RESET(RESET),
    .DESTINATION_SELECTION(clu_helper_categoriser_1_destination_selector),
    .IMM8_2(clu_helper_register_manager_1_imm8_2), .IMM8_1(clu_helper_register_manager_1_imm8_1),
    .INSTRUCTION_OUT(out_17), .REGISTER_DESTINATION(REGISTER_DESTINATION), .REGISTER_2_OUT(REGISTER_2_OUT),
    .REGISTER_1_OUT(REGISTER_1_OUT));
  CLU_Helper_Command clu_helper_command_1 (
    .STACK_IN(STACK_IN), .INSTRUCTION(out_17), .IMM8_1(clu_helper_register_manager_1_imm8_1),
    .IMM8_2(clu_helper_register_manager_1_imm8_2), .R2_IN(R2_IN), .RAM_IN(RAM_IN), .R1_IN(R1_IN),
    .IMM8_OR_REG2(clu_helper_categoriser_1_imm8_reg), .CARRY(clu_helper_command_1_carry), .RESULT(RESULT),
    .JUMP_ADDRESS(clu_helper_command_1_jump_address), .Greater_Than(clu_helper_command_1_greater_than),
    .Equal_Than(clu_helper_command_1_equal_than), .Less_Than(clu_helper_command_1_less_than));
  CLU_Helper_Flag_Manager clu_helper_flag_manager_1 (
    .RESULT(RESULT), .SAVE_TO_REGISTER(SAVE_REGISTER), .CARRY_IN(clu_helper_command_1_carry),
    .CARRY_ENABLE(clu_helper_categoriser_1_carry_enable), .GREATER_IN(clu_helper_command_1_greater_than),
    .LESS_IN(clu_helper_command_1_less_than), .EQUAL_IN(clu_helper_command_1_equal_than),
    .COMPARISION(clu_helper_categoriser_1_compare_flags), .CLOCK(Clock), .RESET(RESET),
    .ZERO_OUT(clu_helper_flag_manager_1_zero_out), .CARRY_OUT(clu_helper_flag_manager_1_carry_out),
    .GREATER_OUT(clu_helper_flag_manager_1_greater_out), .LESS_OUT(clu_helper_flag_manager_1_less_out),
    .EQUAL_OUT(clu_helper_flag_manager_1_equal_out));
  CLU_Helper_Jump_Manager clu_helper_jump_manager_1 (
    .JUMP_COMMAND(clu_helper_categoriser_1_jump_commands), .JUMP_ADDRESS(clu_helper_command_1_jump_address),
    .CALL_ADDRESS(CALL_ADDRESS_IN), .LESS(clu_helper_flag_manager_1_less_out),
    .GREATER(clu_helper_flag_manager_1_greater_out), .EQUAL(clu_helper_flag_manager_1_equal_out),
    .CARRY(clu_helper_flag_manager_1_carry_out), .ZERO(clu_helper_flag_manager_1_zero_out),
    .JUMP_ADDRESS_OUT(JUMP_ADDRESS), .JUMP(clu_helper_jump_manager_1_jump), .CALL(CALL));
  and and_1 (JUMP, clu_helper_cycle_manager_1_third_cycle, clu_helper_jump_manager_1_jump);
endmodule

module CLU_Helper_Command (
  input  [7:0] RAM_IN,
  input  [7:0] R1_IN,
  input  [7:0] IMM8_1,
  input  [7:0] IMM8_2,
  input  [7:0] R2_IN,
  input  IMM8_OR_REG2,
  input  [7:0] STACK_IN,
  input  [7:0] INSTRUCTION,
  output CARRY,
  output [15:0] JUMP_ADDRESS,
  output [7:0] RESULT,
  output Greater_Than,
  output Equal_Than,
  output Less_Than
);

  wire adder_1_cout, adder_2_cout, or_1_out, or_3_out, subtractor_1_bout, subtractor_2_bout;
  wire [7:0] adder_1_out, adder_2_out, and_1_out, divider_1_out, divider_1_rem, multiplexer_1_out,
       multiplexer_2_out, multiplexer_3_out, multiplier_1_out, not_1_out, or_2_out, shifter_1_out,
       shifter_2_out, shifter_3_out, shifter_4_out, shifter_5_out, subtractor_1_out, subtractor_2_out,
       xor_1_out;

  Multiplexer #(.width(8)) multiplexer_1 (.in0(R2_IN), .in1(IMM8_2), .out(multiplexer_1_out), .sel(IMM8_OR_REG2));
  Adder adder_1 (.a(R1_IN), .b(multiplexer_1_out), .out(adder_1_out), .cout(adder_1_cout));  // open: cin
  or or_1 (or_1_out, adder_1_cout, subtractor_1_bout);
  Subtractor subtractor_1 (
    .a(R1_IN), .b(multiplexer_1_out), .out(subtractor_1_out), .bout(subtractor_1_bout));  // open: bin
  Multiplier multiplier_1 (.a(R1_IN), .out(multiplier_1_out));  // open: b, cin, cout
  Divider divider_1 (.a(R1_IN), .out(divider_1_out), .rem(divider_1_rem));  // open: b, upper
  assign and_1_out = R1_IN;  // AND_Gate and_1, 8 bits wide AND_Gate
  assign or_2_out = R1_IN;  // OR_Gate or_2, 8 bits wide OR_Gate
  assign xor_1_out = R1_IN ^ multiplexer_1_out;  // XOR_Gate xor_1, 8 bits wide
  assign not_1_out = ~R1_IN;  // NOT_Gate not_1, 8 bits wide
  Shifter shifter_1 (.in(R1_IN), .\dist (multiplexer_1_out[2:0]), .out(shifter_1_out));
  Shifter #(.shift("lr")) shifter_2 (.in(R1_IN), .\dist (multiplexer_1_out[2:0]), .out(shifter_2_out));
  Shifter #(.shift("rr")) shifter_3 (.in(R1_IN), .\dist (multiplexer_1_out[2:0]), .out(shifter_3_out));
  Shifter #(.shift("rl")) shifter_4 (.in(R1_IN), .\dist (multiplexer_1_out[2:0]), .out(shifter_4_out));
  Shifter #(.shift("ar")) shifter_5 (.in(R1_IN), .\dist (multiplexer_1_out[2:0]), .out(shifter_5_out));
  Comparator comparator_1 (.a(R1_IN), .b(multiplexer_1_out), .gt(Greater_Than), .eq(Equal_Than), .lt(Less_Than));
  Adder adder_2 (.a(R1_IN), .b(8'h1), .out(adder_2_out), .cout(adder_2_cout));  // open: cin
  Subtractor subtractor_2 (.a(R1_IN), .b(8'h1), .out(subtractor_2_out), .bout(subtractor_2_bout));  // open: bin
  or or_3 (or_3_out, adder_2_cout, subtractor_2_bout);
  or or_4 (CARRY, or_1_out, or_3_out);
  Multiplexer #(.select(5), .width(8)) multiplexer_2 (
    .in2(RAM_IN), .in3(R1_IN), .in4(R1_IN), .in5(IMM8_2), .in7(adder_1_out), .in8(subtractor_1_out),
    .in9(multiplier_1_out), .in10(divider_1_out), .in11(divider_1_rem), .in12(and_1_out), .in13(or_2_out),
    .in14(xor_1_out), .in15(not_1_out), .in16(shifter_1_out), .in17(shifter_2_out), .in18(shifter_3_out),
    .in19(shifter_4_out), .in20(shifter_5_out), .in21(adder_1_out), .in22(subtractor_1_out),
    .in23(multiplier_1_out), .in24(divider_1_out), .in25(divider_1_rem), .in26(and_1_out), .in27(or_2_out),
    .in28(xor_1_out), .in29(not_1_out), .in30(shifter_1_out), .in31(shifter_2_out), .out(multiplexer_2_out),
    .sel(INSTRUCTION[4:0]));  // open: in0, in1, in6
  Multiplexer #(.select(5), .width(8)) multiplexer_3 (
    .in0(shifter_3_out), .in1(shifter_4_out), .in2(shifter_5_out), .in3(adder_2_out), .in4(subtractor_2_out),
    .in18(R1_IN), .in19(STACK_IN), .out(multiplexer_3_out), .sel(INSTRUCTION[4:0]));  // open: in5, in6, in7, in8, in9, in10, in11, in12, in13, in14, in15, in16, in17, in20, in21, in22, in23, in24, in25, in26, in27, in28, in29, in30, in31
  Multiplexer #(.width(8)) multiplexer_4 (
    .in0(multiplexer_2_out), .in1(multiplexer_3_out), .out(RESULT), .sel(INSTRUCTION[5]));

  assign JUMP_ADDRESS = {IMM8_1, IMM8_2};

  // Notes on the sheet:
  //   REG2 or IMM8
  //   ST 0x03
  //   MOV 0x04
  //   LI 0x05
  //   LD 0x02
  //   ADD 0x07
  //   SUB 0x08
  //   MULT 0x09
  //   DIV 0x0A
  //   QUOT 0x0B
  //   AND 0x0C
  //   OR 0x0D
  //   XOR 0x0E
  //   NOT 0x0F
  //   SHL 0x10
  //   SHR 0x11
  //   RR 0x12
  //   RL 0x13
  //   Al 0x14
  //   IMM8s
  //   INC 0x23
  //   DEC 0x24
  //   POP 0x33
  //   NOP 0x00
  //   HALT 0x01
  //   PUSH 0x32
endmodule

module CLU_Helper_Categoriser (
  input  FINAL_CYCLE,
  input  [7:0] INSTRUCTION,
  output SAVE_TO_RAM,
  output NOP,
  output HALT,
  output SAVE_VIDEO,
  output SAVE_TO_REGISTER,
  output IMM8_REG,
  output [12:0] JUMP_COMMANDS,
  output COMPARE_FLAGS,
  output RTN,
  output PUSH,
  output POP,
  output CYCLE_1,
  output CYCLE_3,
  output CYCLE_2,
  output CARRY_ENABLE,
  output [1:0] DESTINATION_SELECTOR
);

  wire demultiplexer_1_out2, demultiplexer_1_out3, demultiplexer_1_out4, demultiplexer_1_out5,
       demultiplexer_1_out6, demultiplexer_1_out7, demultiplexer_1_out8, demultiplexer_1_out9,
       demultiplexer_1_out10, demultiplexer_1_out11, demultiplexer_1_out12, demultiplexer_1_out13,
       demultiplexer_1_out14, demultiplexer_1_out15, demultiplexer_1_out16, demultiplexer_1_out17,
       demultiplexer_1_out18, demultiplexer_1_out19, demultiplexer_1_out20, demultiplexer_1_out21,
       demultiplexer_1_out22, demultiplexer_1_out23, demultiplexer_1_out24, demultiplexer_1_out25,
       demultiplexer_1_out26, demultiplexer_1_out27, demultiplexer_1_out28, demultiplexer_1_out29,
       demultiplexer_1_out30, demultiplexer_1_out31, demultiplexer_2_out0, demultiplexer_2_out1,
       demultiplexer_2_out2, demultiplexer_2_out3, demultiplexer_2_out4, demultiplexer_2_out17,
       demultiplexer_2_out18, demultiplexer_2_out19, demultiplexer_2_out20, demultiplexer_2_out21,
       demultiplexer_3_out0, demultiplexer_3_out1, demultiplexer_3_out4, demultiplexer_3_out6,
       demultiplexer_3_out15, demultiplexer_4_out3, demultiplexer_4_out4, demultiplexer_4_out17,
       demultiplexer_4_out18, demultiplexer_4_out19, demultiplexer_4_out20, demultiplexer_5_out3,
       demultiplexer_5_out4, demultiplexer_5_out5, demultiplexer_5_out7, demultiplexer_5_out8,
       demultiplexer_5_out15, demultiplexer_5_out21, demultiplexer_5_out22, demultiplexer_5_out23,
       demultiplexer_5_out24, demultiplexer_5_out25, demultiplexer_5_out26, demultiplexer_5_out27,
       demultiplexer_5_out28, demultiplexer_5_out29, demultiplexer_5_out30, demultiplexer_5_out31,
       demultiplexer_6_out0, demultiplexer_6_out1, demultiplexer_6_out2, demultiplexer_6_out3,
       demultiplexer_6_out4, demultiplexer_6_out18, demultiplexer_6_out19, not_1_out, not_2_out, not_3_out,
       one_out, or_1_out, or_2_out, or_3_out, or_7_out, or_10_out, or_11_out, three_out, two_out;

  not not_1 (not_1_out, INSTRUCTION[5]);
  not not_2 (not_2_out, INSTRUCTION[5]);
  not not_3 (not_3_out, INSTRUCTION[5]);
  Demultiplexer #(.select(5)) demultiplexer_1 (
    .out0(NOP), .out1(HALT), .out2(demultiplexer_1_out2), .out3(demultiplexer_1_out3),
    .out4(demultiplexer_1_out4), .out5(demultiplexer_1_out5), .out6(demultiplexer_1_out6),
    .out7(demultiplexer_1_out7), .out8(demultiplexer_1_out8), .out9(demultiplexer_1_out9),
    .out10(demultiplexer_1_out10), .out11(demultiplexer_1_out11), .out12(demultiplexer_1_out12),
    .out13(demultiplexer_1_out13), .out14(demultiplexer_1_out14), .out15(demultiplexer_1_out15),
    .out16(demultiplexer_1_out16), .out17(demultiplexer_1_out17), .out18(demultiplexer_1_out18),
    .out19(demultiplexer_1_out19), .out20(demultiplexer_1_out20), .out21(demultiplexer_1_out21),
    .out22(demultiplexer_1_out22), .out23(demultiplexer_1_out23), .out24(demultiplexer_1_out24),
    .out25(demultiplexer_1_out25), .out26(demultiplexer_1_out26), .out27(demultiplexer_1_out27),
    .out28(demultiplexer_1_out28), .out29(demultiplexer_1_out29), .out30(demultiplexer_1_out30),
    .out31(demultiplexer_1_out31), .in(not_1_out), .sel(INSTRUCTION[4:0]));
  Demultiplexer #(.select(5)) demultiplexer_2 (
    .out0(demultiplexer_2_out0), .out1(demultiplexer_2_out1), .out2(demultiplexer_2_out2),
    .out3(demultiplexer_2_out3), .out4(demultiplexer_2_out4), .out5(JUMP_COMMANDS[0]),
    .out6(JUMP_COMMANDS[1]), .out7(JUMP_COMMANDS[2]), .out8(JUMP_COMMANDS[3]), .out9(JUMP_COMMANDS[4]),
    .out10(JUMP_COMMANDS[5]), .out11(JUMP_COMMANDS[6]), .out12(JUMP_COMMANDS[7]), .out13(JUMP_COMMANDS[8]),
    .out14(JUMP_COMMANDS[9]), .out15(JUMP_COMMANDS[10]), .out16(JUMP_COMMANDS[11]),
    .out17(demultiplexer_2_out17), .out18(demultiplexer_2_out18), .out19(demultiplexer_2_out19),
    .out20(demultiplexer_2_out20), .out21(demultiplexer_2_out21), .in(INSTRUCTION[5]), .sel(INSTRUCTION[4:0]));  // open: out22, out23, out24, out25, out26, out27, out28, out29, out30, out31
  Demultiplexer #(.select(5)) demultiplexer_3 (
    .out0(demultiplexer_3_out0), .out1(demultiplexer_3_out1), .out4(demultiplexer_3_out4),
    .out6(demultiplexer_3_out6), .out15(demultiplexer_3_out15), .in(not_2_out), .sel(INSTRUCTION[4:0]));  // open: out2, out3, out5, out7, out8, out9, out10, out11, out12, out13, out14, out16, out17, out18, out19, out20, out21, out22, out23, out24, out25, out26, out27, out28, out29, out30, out31
  Demultiplexer #(.select(5)) demultiplexer_4 (
    .out3(demultiplexer_4_out3), .out4(demultiplexer_4_out4), .out17(demultiplexer_4_out17),
    .out18(demultiplexer_4_out18), .out19(demultiplexer_4_out19), .out20(demultiplexer_4_out20),
    .in(INSTRUCTION[5]), .sel(INSTRUCTION[4:0]));  // open: out0, out1, out2, out5, out6, out7, out8, out9, out10, out11, out12, out13, out14, out15, out16, out21, out22, out23, out24, out25, out26, out27, out28, out29, out30, out31
  Demultiplexer #(.select(5)) demultiplexer_5 (
    .out3(demultiplexer_5_out3), .out4(demultiplexer_5_out4), .out5(demultiplexer_5_out5),
    .out7(demultiplexer_5_out7), .out8(demultiplexer_5_out8), .out15(demultiplexer_5_out15),
    .out21(demultiplexer_5_out21), .out22(demultiplexer_5_out22), .out23(demultiplexer_5_out23),
    .out24(demultiplexer_5_out24), .out25(demultiplexer_5_out25), .out26(demultiplexer_5_out26),
    .out27(demultiplexer_5_out27), .out28(demultiplexer_5_out28), .out29(demultiplexer_5_out29),
    .out30(demultiplexer_5_out30), .out31(demultiplexer_5_out31), .in(not_3_out), .sel(INSTRUCTION[4:0]));  // open: out0, out1, out2, out6, out9, out10, out11, out12, out13, out14, out16, out17, out18, out19, out20
  Demultiplexer #(.select(5)) demultiplexer_6 (
    .out0(demultiplexer_6_out0), .out1(demultiplexer_6_out1), .out2(demultiplexer_6_out2),
    .out3(demultiplexer_6_out3), .out4(demultiplexer_6_out4), .out18(demultiplexer_6_out18),
    .out19(demultiplexer_6_out19), .in(INSTRUCTION[5]), .sel(INSTRUCTION[4:0]));  // open: out5, out6, out7, out8, out9, out10, out11, out12, out13, out14, out15, out16, out17, out20, out21, out22, out23, out24, out25, out26, out27, out28, out29, out30, out31
  and and_1 (RTN, demultiplexer_2_out17, FINAL_CYCLE);
  or or_1 (or_1_out, demultiplexer_1_out21, demultiplexer_1_out22, demultiplexer_1_out23, demultiplexer_1_out24, demultiplexer_1_out25, demultiplexer_1_out26, demultiplexer_1_out27, demultiplexer_1_out28, demultiplexer_1_out29, demultiplexer_1_out30, demultiplexer_1_out31);
  or or_2 (or_2_out, demultiplexer_2_out0, demultiplexer_2_out1, demultiplexer_2_out2);
  and and_2 (POP, demultiplexer_2_out19, FINAL_CYCLE);
  and and_3 (SAVE_TO_RAM, FINAL_CYCLE, demultiplexer_1_out3);
  or or_3 (or_3_out, demultiplexer_1_out7, demultiplexer_1_out8, demultiplexer_1_out9, demultiplexer_1_out10, demultiplexer_1_out11, demultiplexer_1_out12, demultiplexer_1_out13, demultiplexer_1_out15, demultiplexer_1_out16, demultiplexer_1_out17, demultiplexer_1_out18, demultiplexer_1_out19, demultiplexer_1_out20);
  or or_4 (COMPARE_FLAGS, demultiplexer_2_out20, demultiplexer_2_out21);
  and and_4 (PUSH, demultiplexer_2_out18, FINAL_CYCLE);
  or or_5 (CYCLE_1, demultiplexer_3_out0, demultiplexer_3_out1, demultiplexer_3_out6, demultiplexer_4_out17);
  or or_6 (CYCLE_2, demultiplexer_3_out4, demultiplexer_3_out15, demultiplexer_4_out3, demultiplexer_4_out4, demultiplexer_4_out18, demultiplexer_4_out19, demultiplexer_4_out20);
  or two (two_out, demultiplexer_5_out15, demultiplexer_5_out21, demultiplexer_5_out22, demultiplexer_5_out23, demultiplexer_5_out24, demultiplexer_5_out25, demultiplexer_5_out26, demultiplexer_5_out27, demultiplexer_5_out28, demultiplexer_5_out30, demultiplexer_5_out31, demultiplexer_6_out0, demultiplexer_6_out1, demultiplexer_6_out2, demultiplexer_6_out3, demultiplexer_6_out4);
  or one (one_out, demultiplexer_5_out3, demultiplexer_5_out4, demultiplexer_5_out5, demultiplexer_5_out29, demultiplexer_6_out18, demultiplexer_6_out19);
  or or_7 (or_7_out, demultiplexer_1_out2, demultiplexer_1_out4, demultiplexer_1_out5);
  or or_8 (IMM8_REG, demultiplexer_1_out5, or_1_out, demultiplexer_2_out21, or_2_out);
  and and_5 (CYCLE_3, ~CYCLE_1, ~CYCLE_2);  // AND_Gate
  or or_9 (CARRY_ENABLE, demultiplexer_5_out7, demultiplexer_5_out8, demultiplexer_5_out21, demultiplexer_5_out22, demultiplexer_6_out3, demultiplexer_6_out4);
  or or_10 (or_10_out, demultiplexer_2_out3, demultiplexer_2_out4);
  and three (three_out, ~two_out, ~one_out);  // AND_Gate
  and and_6 (SAVE_VIDEO, FINAL_CYCLE, demultiplexer_1_out6);
  Priority_Encoder #(.select(2)) priority_encoder_1 (
    .in0(one_out), .in1(two_out), .in2(three_out), .in3(1'b0), .out(DESTINATION_SELECTOR));  // open: gs, en_out, en_in
  or or_11 (or_11_out, or_7_out, or_3_out, or_10_out, demultiplexer_2_out18);
  and and_7 (SAVE_TO_REGISTER, FINAL_CYCLE, or_11_out);

  assign JUMP_COMMANDS[12] = FINAL_CYCLE;
endmodule

module CLU_Helper_Jump_Manager (
  input  CARRY,
  input  ZERO,
  input  LESS,
  input  GREATER,
  input  EQUAL,
  input  [15:0] JUMP_ADDRESS,
  input  [15:0] CALL_ADDRESS,
  input  [12:0] JUMP_COMMAND,
  output JUMP,
  output CALL,
  output [15:0] JUMP_ADDRESS_OUT
);

  wire and_1_out, and_2_out, and_3_out, and_4_out, and_5_out, and_6_out, and_7_out, and_8_out, and_9_out,
       and_10_out, or_1_out;

  or or_1 (or_1_out, LESS, EQUAL);
  and and_1 (and_1_out, ~CARRY, JUMP_COMMAND[10]);  // AND_Gate
  and and_2 (and_2_out, CARRY, JUMP_COMMAND[9]);
  and and_3 (and_3_out, ~ZERO, JUMP_COMMAND[8]);  // AND_Gate
  and and_4 (and_4_out, ZERO, JUMP_COMMAND[7]);
  and and_5 (and_5_out, or_1_out, JUMP_COMMAND[6]);
  and and_6 (and_6_out, GREATER, JUMP_COMMAND[5]);
  and and_7 (and_7_out, LESS, JUMP_COMMAND[4]);
  and and_8 (and_8_out, GREATER, JUMP_COMMAND[3]);
  and and_9 (and_9_out, ~EQUAL, JUMP_COMMAND[2]);  // AND_Gate
  and and_10 (and_10_out, EQUAL, JUMP_COMMAND[1]);
  or or_2 (JUMP, and_6_out, and_1_out, and_2_out, and_3_out, and_4_out, and_5_out, and_7_out, and_8_out, and_9_out, and_10_out, JUMP_COMMAND[0], JUMP_COMMAND[11]);
  Multiplexer #(.width(16)) multiplexer_1 (
    .in0(JUMP_ADDRESS), .in1(CALL_ADDRESS), .out(JUMP_ADDRESS_OUT), .sel(JUMP_COMMAND[11]));

  assign CALL = JUMP_COMMAND[11];

  // Notes on the sheet:
  //   JMP Not Carry Flag
  //   JMP Not Zero Flag
  //   JMP Less or Equal
  //   JMP Greater or Equal
  //   JMP Carry Flag
  //   JMP Zero Flag
  //   JMP Less
  //   JMP Greater
  //   JMP Not Equal
  //   JMP Equal
  //   JMP Absoute
endmodule

module CLU_Helper_Flag_Manager (
  input  [7:0] RESULT,
  input  SAVE_TO_REGISTER,
  input  CARRY_IN,
  input  CARRY_ENABLE,
  input  GREATER_IN,
  input  LESS_IN,
  input  EQUAL_IN,
  input  COMPARISION,
  input  CLOCK,
  input  RESET,
  output ZERO_OUT,
  output CARRY_OUT,
  output GREATER_OUT,
  output LESS_OUT,
  output EQUAL_OUT
);

  wire nand_1_out;

  nand nand_1 (nand_1_out, RESULT[3], RESULT[0], RESULT[1], RESULT[2], RESULT[4], RESULT[5], RESULT[6], RESULT[7]);
  Register #(.width(1)) ZERO (.D(nand_1_out), .en(SAVE_TO_REGISTER), .clk(CLOCK), .Q(ZERO_OUT), .clr(RESET));
  Register #(.width(1)) CARRY (.D(CARRY_IN), .en(CARRY_ENABLE), .clk(CLOCK), .Q(CARRY_OUT), .clr(RESET));
  Register #(.width(1)) GREATER (.D(GREATER_IN), .en(COMPARISION), .clk(CLOCK), .Q(GREATER_OUT), .clr(RESET));
  Register #(.width(1)) LESS (.D(LESS_IN), .en(COMPARISION), .clk(CLOCK), .Q(LESS_OUT), .clr(RESET));
  Register #(.width(1)) EQUAL (.D(EQUAL_IN), .en(COMPARISION), .clk(CLOCK), .Q(EQUAL_OUT), .clr(RESET));
endmodule

module CLU_Helper_Cycle_Manager (
  input  CYCLE_2,
  input  CYCLE_1,
  input  CLOCK,
  input  RESET,
  output FIRST_CYCLE,
  output FINAL_CYCLE,
  output SECOND_CYCLE,
  output THIRD_CYCLE
);

  wire and_2_out, and_3_out, and_4_out, and_5_out, and_6_out, and_7_out, or_1_out, or_2_out;

  T_Flip_Flop t_ff_1 (.T(CLOCK), .clk(CLOCK), .Q(SECOND_CYCLE), .reset(or_1_out));  // open: Qn, preset
  and and_1 (FIRST_CYCLE, ~SECOND_CYCLE, ~THIRD_CYCLE);  // AND_Gate
  T_Flip_Flop t_ff_2 (.T(SECOND_CYCLE), .clk(CLOCK), .Q(THIRD_CYCLE), .reset(or_1_out));  // open: Qn, preset
  or or_1 (or_1_out, or_2_out, RESET);
  and and_2 (and_2_out, CYCLE_2, THIRD_CYCLE);
  and and_3 (and_3_out, SECOND_CYCLE, THIRD_CYCLE);
  and and_4 (and_4_out, SECOND_CYCLE, CYCLE_1);
  or or_2 (or_2_out, and_4_out, and_2_out, and_3_out);
  and and_5 (and_5_out, CYCLE_1, FIRST_CYCLE);
  and and_6 (and_6_out, CYCLE_2, SECOND_CYCLE);
  and and_7 (and_7_out, ~CYCLE_1, ~CYCLE_2, THIRD_CYCLE);  // AND_Gate
  or or_3 (FINAL_CYCLE, and_5_out, and_6_out, and_7_out);
endmodule

module CLU_Helper_Register_Manager (
  input  [1:0] DESTINATION_SELECTION,
  input  [7:0] INSTRUCTION_BUS,
  input  THIRD_CYCLE,
  input  SECOND_CYCLE,
  input  CLOCK,
  input  FIRST_CYCLE,
  input  RESET,
  output [3:0] REGISTER_DESTINATION,
  output [7:0] IMM8_2,
  output [3:0] REGISTER_2_OUT,
  output [3:0] REGISTER_1_OUT,
  output [7:0] IMM8_1,
  output [7:0] INSTRUCTION_OUT
);

  Register VALUE_2 (.D(INSTRUCTION_BUS), .en(THIRD_CYCLE), .clk(THIRD_CYCLE), .Q(IMM8_2), .clr(RESET));
  Register VALUE_1 (.D(INSTRUCTION_BUS), .en(SECOND_CYCLE), .clk(SECOND_CYCLE), .Q(IMM8_1), .clr(RESET));
  Register INSTRUCTION (.D(INSTRUCTION_BUS), .en(FIRST_CYCLE), .clk(FIRST_CYCLE), .Q(INSTRUCTION_OUT), .clr(RESET));
  Multiplexer #(.select(2), .width(4)) multiplexer_1 (
    .in0(IMM8_1[7:4]), .in1(IMM8_1[3:0]), .in2(IMM8_2[7:4]), .in3(IMM8_2[3:0]), .out(REGISTER_DESTINATION),
    .sel(DESTINATION_SELECTION));

  assign REGISTER_1_OUT = IMM8_1[7:4];
  assign REGISTER_2_OUT = IMM8_1[3:0];
endmodule

module CALL_STACK_16x16 (
  input  CLOCK,
  input  [15:0] INPUT_16,
  input  CALL,
  input  RTRN,
  output [3:0] ADDRESS,
  output [15:0] OUT_16,
  output WRITE_ENABLE
);

  wire or_1_out;

  or or_1 (or_1_out, CALL, RTRN);
  and and_1 (WRITE_ENABLE, CLOCK, or_1_out);
  INC_DEC_FOUR_BIT_COUNTER inc_dec_four_bit_counter_1 (
    .clk(WRITE_ENABLE), .shf(RTRN), .OUTPUTS(ADDRESS));  // open: BORROW, CARRY
  Multiplexer #(.width(16)) multiplexer_1 (.in0(INPUT_16), .in1({16{1'b0}}), .out(OUT_16), .sel(RTRN));
endmodule

module PUSH_POP_STACK_256x8 (
  input  CLOCK,
  input  [7:0] INPUT_8,
  input  PUSH,
  input  POP,
  output [7:0] ADDRESS,
  output [7:0] OUT_8,
  output WRITE_ENABLE
);

  wire or_1_out;

  and and_1 (WRITE_ENABLE, CLOCK, or_1_out);
  or or_1 (or_1_out, PUSH, POP);
  INC_DEC_EIGHT_BIT_COUNTER inc_dec_eight_bit_counter_1 (
    .CLOCK(WRITE_ENABLE), .INC_DEC(POP), .NUM(ADDRESS));  // open: CARRY, BORROW
  Multiplexer #(.width(8)) multiplexer_1 (.in0(INPUT_8), .in1({8{1'b0}}), .out(OUT_8), .sel(POP));
endmodule
